// Digital circuit 8 bit ALU logic gates.dig as structural Verilog
module _8_bit_ALU_logic_gates (
  input  in_1,
  input  in_2
);

  wire Addition___Subjection_out, and_1_out, and_2_out, and_3_out, and_4_out, and_5_out, and_6_out,
       and_7_out, and_8_out, and_9_out, and_10_out, and_11_out, and_12_out, and_13_out, and_14_out,
       and_15_out, and_16_out, and_17_out, and_18_out, and_19_out, and_20_out, and_21_out, and_22_out,
       and_23_out, and_24_out, and_25_out, and_26_out, and_27_out, and_28_out, and_29_out, and_30_out,
       and_31_out, and_32_out, not_1_out, not_2_out, not_3_out, not_4_out, not_5_out, not_6_out, not_7_out,
       not_8_out, not_9_out, not_10_out, not_11_out, not_12_out, not_13_out, not_14_out, not_15_out,
       not_16_out, or_1_out, or_2_out, or_3_out, or_4_out, or_5_out, or_6_out, or_7_out, or_8_out, or_9_out,
       or_10_out, or_11_out, or_12_out, or_13_out, or_14_out, or_15_out, or_16_out, xor_1_out, xor_2_out,
       xor_3_out, xor_4_out, xor_5_out, xor_6_out, xor_7_out, xor_8_out, xor_17_out, xor_18_out, xor_19_out,
       xor_20_out, xor_21_out, xor_22_out, xor_23_out, xor_24_out;
  wire [7:0] dipswitch_1_out, dipswitch_9_out, multiplexer_1_out, xor_16_out, xor_25_out;

  xor xor_1 (xor_1_out, dipswitch_1_out[0], dipswitch_9_out[0]);
  xor xor_2 (xor_2_out, dipswitch_1_out[1], dipswitch_9_out[1]);
  xor xor_3 (xor_3_out, dipswitch_1_out[2], dipswitch_9_out[2]);
  xor xor_4 (xor_4_out, dipswitch_1_out[3], dipswitch_9_out[3]);
  xor xor_5 (xor_5_out, dipswitch_1_out[4], dipswitch_9_out[4]);
  xor xor_6 (xor_6_out, dipswitch_1_out[5], dipswitch_9_out[5]);
  xor xor_7 (xor_7_out, dipswitch_1_out[6], dipswitch_9_out[6]);
  xor xor_8 (xor_8_out, dipswitch_1_out[7], dipswitch_9_out[7]);
  xor xor_9 (xor_16_out[0], xor_1_out, in_2);
  and and_1 (and_1_out, in_2, xor_1_out);
  and and_2 (and_2_out, dipswitch_9_out[0], dipswitch_1_out[0]);
  xor xor_10 (xor_16_out[1], xor_2_out, or_1_out);
  and and_3 (and_3_out, or_1_out, xor_2_out);
  and and_4 (and_4_out, dipswitch_9_out[1], dipswitch_1_out[1]);
  xor xor_11 (xor_16_out[2], xor_3_out, or_2_out);
  and and_5 (and_5_out, or_2_out, xor_3_out);
  and and_6 (and_6_out, dipswitch_9_out[2], dipswitch_1_out[2]);
  xor xor_12 (xor_16_out[3], xor_4_out, or_3_out);
  and and_7 (and_7_out, or_3_out, xor_4_out);
  and and_8 (and_8_out, dipswitch_9_out[3], dipswitch_1_out[3]);
  xor xor_13 (xor_16_out[4], xor_5_out, or_4_out);
  and and_9 (and_9_out, or_4_out, xor_5_out);
  and and_10 (and_10_out, dipswitch_9_out[4], dipswitch_1_out[4]);
  xor xor_14 (xor_16_out[5], xor_6_out, or_5_out);
  and and_11 (and_11_out, or_5_out, xor_6_out);
  and and_12 (and_12_out, dipswitch_9_out[5], dipswitch_1_out[5]);
  xor xor_15 (xor_16_out[6], xor_7_out, or_6_out);
  and and_13 (and_13_out, or_6_out, xor_7_out);
  and and_14 (and_14_out, dipswitch_9_out[6], dipswitch_1_out[6]);
  xor xor_16 (xor_16_out[7], xor_8_out, or_7_out);
  and and_15 (and_15_out, or_7_out, xor_8_out);
  and and_16 (and_16_out, dipswitch_9_out[7], dipswitch_1_out[7]);
  or or_1 (or_1_out, and_1_out, and_2_out);
  or or_2 (or_2_out, and_3_out, and_4_out);
  or or_3 (or_3_out, and_5_out, and_6_out);
  or or_4 (or_4_out, and_7_out, and_8_out);
  or or_5 (or_5_out, and_9_out, and_10_out);
  or or_6 (or_6_out, and_11_out, and_12_out);
  or or_7 (or_7_out, and_13_out, and_14_out);
  or or_8 (or_8_out, and_15_out, and_16_out);
  xor xor_17 (xor_17_out, dipswitch_1_out[0], dipswitch_9_out[0]);
  not not_1 (not_1_out, dipswitch_1_out[0]);
  xor xor_18 (xor_18_out, dipswitch_1_out[1], dipswitch_9_out[1]);
  not not_2 (not_2_out, dipswitch_1_out[1]);
  xor xor_19 (xor_19_out, dipswitch_1_out[2], dipswitch_9_out[2]);
  not not_3 (not_3_out, dipswitch_1_out[2]);
  xor xor_20 (xor_20_out, dipswitch_1_out[3], dipswitch_9_out[3]);
  not not_4 (not_4_out, dipswitch_1_out[3]);
  xor xor_21 (xor_21_out, dipswitch_1_out[4], dipswitch_9_out[4]);
  not not_5 (not_5_out, dipswitch_1_out[4]);
  xor xor_22 (xor_22_out, dipswitch_1_out[5], dipswitch_9_out[5]);
  not not_6 (not_6_out, dipswitch_1_out[5]);
  xor xor_23 (xor_23_out, dipswitch_1_out[6], dipswitch_9_out[6]);
  not not_7 (not_7_out, dipswitch_1_out[6]);
  xor xor_24 (xor_24_out, dipswitch_1_out[7], dipswitch_9_out[7]);
  not not_8 (not_8_out, dipswitch_1_out[7]);
  not not_9 (not_9_out, xor_17_out);
  not not_10 (not_10_out, xor_18_out);
  not not_11 (not_11_out, xor_19_out);
  not not_12 (not_12_out, xor_20_out);
  not not_13 (not_13_out, xor_21_out);
  not not_14 (not_14_out, xor_22_out);
  not not_15 (not_15_out, xor_23_out);
  not not_16 (not_16_out, xor_24_out);
  xor xor_25 (xor_25_out[0], xor_17_out, in_1);
  and and_17 (and_17_out, in_1, not_9_out);
  and and_18 (and_18_out, dipswitch_9_out[0], not_1_out);
  xor xor_26 (xor_25_out[1], xor_18_out, or_9_out);
  and and_19 (and_19_out, or_9_out, not_10_out);
  and and_20 (and_20_out, dipswitch_9_out[1], not_2_out);
  xor xor_27 (xor_25_out[2], xor_19_out, or_10_out);
  and and_21 (and_21_out, or_10_out, not_11_out);
  and and_22 (and_22_out, dipswitch_9_out[2], not_3_out);
  xor xor_28 (xor_25_out[3], xor_20_out, or_11_out);
  and and_23 (and_23_out, or_11_out, not_12_out);
  and and_24 (and_24_out, dipswitch_9_out[3], not_4_out);
  xor xor_29 (xor_25_out[4], xor_21_out, or_12_out);
  and and_25 (and_25_out, or_12_out, not_13_out);
  and and_26 (and_26_out, dipswitch_9_out[4], not_5_out);
  xor xor_30 (xor_25_out[5], xor_22_out, or_13_out);
  and and_27 (and_27_out, or_13_out, not_14_out);
  and and_28 (and_28_out, dipswitch_9_out[5], not_6_out);
  xor xor_31 (xor_25_out[6], xor_23_out, or_14_out);
  and and_29 (and_29_out, or_14_out, not_15_out);
  and and_30 (and_30_out, dipswitch_9_out[6], not_7_out);
  xor xor_32 (xor_25_out[7], xor_24_out, or_15_out);
  and and_31 (and_31_out, or_15_out, not_16_out);
  and and_32 (and_32_out, dipswitch_9_out[7], not_8_out);
  or or_9 (or_9_out, and_17_out, and_18_out);
  or or_10 (or_10_out, and_19_out, and_20_out);
  or or_11 (or_11_out, and_21_out, and_22_out);
  or or_12 (or_12_out, and_23_out, and_24_out);
  or or_13 (or_13_out, and_25_out, and_26_out);
  or or_14 (or_14_out, and_27_out, and_28_out);
  or or_15 (or_15_out, and_29_out, and_30_out);
  or or_16 (or_16_out, and_31_out, and_32_out);
  Multiplexer #(.Bits(8)) multiplexer_1 (
    .sel(Addition___Subjection_out), .in_0(xor_16_out), .in_1(xor_25_out), .out(multiplexer_1_out));
  DipSwitch dipswitch_1 (.out(dipswitch_1_out[0]));
  DipSwitch dipswitch_2 (.out(dipswitch_1_out[1]));
  DipSwitch dipswitch_3 (.out(dipswitch_1_out[2]));
  DipSwitch dipswitch_4 (.out(dipswitch_1_out[3]));
  DipSwitch dipswitch_5 (.out(dipswitch_1_out[4]));
  LED led_1 (.in(multiplexer_1_out[0]));
  DipSwitch dipswitch_6 (.out(dipswitch_1_out[5]));
  DipSwitch dipswitch_7 (.out(dipswitch_1_out[6]));
  LED led_2 (.in(multiplexer_1_out[1]));
  LED led_3 (.in(multiplexer_1_out[2]));
  DipSwitch dipswitch_8 (.out(dipswitch_1_out[7]));
  LED led_4 (.in(multiplexer_1_out[3]));
  LED led_5 (.in(multiplexer_1_out[4]));
  DipSwitch dipswitch_9 (.out(dipswitch_9_out[0]));
  DipSwitch dipswitch_10 (.out(dipswitch_9_out[1]));
  LED led_6 (.in(multiplexer_1_out[5]));
  LED led_7 (.in(multiplexer_1_out[6]));
  DipSwitch dipswitch_11 (.out(dipswitch_9_out[2]));
  DipSwitch dipswitch_12 (.out(dipswitch_9_out[3]));
  LED led_8 (.in(multiplexer_1_out[7]));
  DipSwitch dipswitch_13 (.out(dipswitch_9_out[4]));
  DipSwitch dipswitch_14 (.out(dipswitch_9_out[5]));
  DipSwitch dipswitch_15 (.out(dipswitch_9_out[6]));
  DipSwitch dipswitch_16 (.out(dipswitch_9_out[7]));
  DipSwitch Addition___Subjection (.out(Addition___Subjection_out));

  // Notes on the sheet:
  //   First number
  //   Second number
endmodule
