// Digital circuit 8 bit ALU no logic gates.dig as structural Verilog
module _8_bit_ALU_no_logic_gates (
  input  in_1,
  input  in_2,
  input  in_3
);

  wire add_1_c_o, add_2_c_o, add_3_c_o, add_5_c_o, add_6_c_o, add_8_c_o, add_9_c_o,
       Addition___Subjection_out, and_1_out, and_2_out, and_3_out, and_4_out, and_5_out, and_6_out,
       and_7_out, and_8_out, and_9_out, and_10_out, and_11_out, and_12_out, and_13_out, and_14_out,
       and_15_out, and_16_out, not_1_out, not_2_out, not_3_out, not_4_out, not_5_out, not_6_out, not_7_out,
       not_8_out, not_9_out, not_10_out, or_1_out, or_2_out, or_3_out, or_4_out, or_5_out, or_6_out,
       or_7_out, or_8_out, sub_1_c_o, sub_2_c_o, sub_3_c_o, sub_4_c_o, sub_5_c_o, sub_6_c_o, sub_7_c_o,
       undriven, undriven_2, undriven_3, undriven_4, undriven_5, undriven_6, undriven_7, undriven_8,
       undriven_9, undriven_10, undriven_11, undriven_12, undriven_13, undriven_14, undriven_15, undriven_16,
       xor_1_out, xor_2_out, xor_3_out, xor_4_out, xor_5_out, xor_6_out, xor_7_out, xor_8_out, xor_9_out,
       xor_10_out, xor_11_out, xor_12_out, xor_13_out, xor_14_out, xor_15_out, xor_16_out;
  wire [7:0] add_1_s, dipswitch_1_out, dipswitch_9_out, multiplexer_1_out, sub_1_s;

  not not_1 (not_1_out, undriven_4);
  not not_2 (not_2_out, undriven_3);
  xor xor_1 (xor_1_out, undriven_16, undriven_8);
  xor xor_2 (xor_2_out, undriven_15, undriven_7);
  xor xor_3 (xor_3_out, undriven_14, undriven_6);
  xor xor_4 (xor_4_out, undriven_13, undriven_5);
  xor xor_5 (xor_5_out, undriven_12, undriven_4);
  xor xor_6 (xor_6_out, undriven_11, undriven_3);
  xor xor_7 (xor_7_out, undriven_10, undriven_2);
  xor xor_8 (xor_8_out, undriven_9, undriven);
  Add add_1 (.a(dipswitch_1_out[7]), .b(dipswitch_9_out[7]), .c_i(in_2), .s(add_1_s[7]), .c_o(add_1_c_o));
  Sub sub_1 (.a(dipswitch_1_out[7]), .b(dipswitch_9_out[7]), .c_i(in_1), .s(sub_1_s[7]), .c_o(sub_1_c_o));
  not not_3 (not_3_out, xor_1_out);
  not not_4 (not_4_out, xor_2_out);
  not not_5 (not_5_out, xor_3_out);
  not not_6 (not_6_out, xor_4_out);
  not not_7 (not_7_out, xor_5_out);
  not not_8 (not_8_out, xor_6_out);
  not not_9 (not_9_out, xor_7_out);
  not not_10 (not_10_out, xor_8_out);
  Add add_2 (.a(dipswitch_1_out[6]), .b(dipswitch_9_out[6]), .c_i(add_1_c_o), .s(add_1_s[6]), .c_o(add_2_c_o));
  Sub sub_2 (.a(dipswitch_1_out[6]), .b(dipswitch_9_out[6]), .c_i(sub_1_c_o), .s(sub_1_s[6]), .c_o(sub_2_c_o));
  xor xor_9 (xor_9_out, xor_1_out, in_3);
  and and_1 (and_1_out, in_3, not_3_out);
  and and_2 (and_2_out, undriven_8, undriven_16);
  xor xor_10 (xor_10_out, xor_2_out, or_1_out);
  and and_3 (and_3_out, or_1_out, not_4_out);
  and and_4 (and_4_out, undriven_7, undriven_15);
  xor xor_11 (xor_11_out, xor_3_out, or_2_out);
  and and_5 (and_5_out, or_2_out, not_5_out);
  and and_6 (and_6_out, undriven_6, undriven_14);
  xor xor_12 (xor_12_out, xor_4_out, or_3_out);
  and and_7 (and_7_out, or_3_out, not_6_out);
  and and_8 (and_8_out, undriven_5, undriven_13);
  xor xor_13 (xor_13_out, xor_5_out, or_4_out);
  and and_9 (and_9_out, or_4_out, not_7_out);
  and and_10 (and_10_out, undriven_4, not_1_out);
  xor xor_14 (xor_14_out, xor_6_out, or_5_out);
  and and_11 (and_11_out, or_5_out, not_8_out);
  and and_12 (and_12_out, undriven_3, not_2_out);
  xor xor_15 (xor_15_out, xor_7_out, or_6_out);
  and and_13 (and_13_out, or_6_out, not_9_out);
  and and_14 (and_14_out, undriven_2, undriven_10);
  xor xor_16 (xor_16_out, xor_8_out, or_7_out);
  and and_15 (and_15_out, or_7_out, not_10_out);
  and and_16 (and_16_out, undriven, undriven_9);
  or or_1 (or_1_out, and_1_out, and_2_out);
  or or_2 (or_2_out, and_3_out, and_4_out);
  or or_3 (or_3_out, and_5_out, and_6_out);
  or or_4 (or_4_out, and_7_out, and_8_out);
  or or_5 (or_5_out, and_9_out, and_10_out);
  or or_6 (or_6_out, and_11_out, and_12_out);
  or or_7 (or_7_out, and_13_out, and_14_out);
  or or_8 (or_8_out, and_15_out, and_16_out);
  Add add_3 (.a(dipswitch_1_out[5]), .b(dipswitch_9_out[5]), .c_i(add_2_c_o), .s(add_1_s[5]), .c_o(add_3_c_o));
  Add add_4 (.a(dipswitch_1_out[5]), .b(dipswitch_9_out[5]), .c_i(add_2_c_o), .s(add_1_s[5]), .c_o(add_3_c_o));
  Sub sub_3 (.a(dipswitch_1_out[5]), .b(dipswitch_9_out[5]), .c_i(sub_2_c_o), .s(sub_1_s[5]), .c_o(sub_3_c_o));
  Add add_5 (.a(dipswitch_1_out[4]), .b(dipswitch_9_out[4]), .c_i(add_3_c_o), .s(add_1_s[4]), .c_o(add_5_c_o));
  Sub sub_4 (.a(dipswitch_1_out[4]), .b(dipswitch_9_out[4]), .c_i(sub_3_c_o), .s(sub_1_s[4]), .c_o(sub_4_c_o));
  Add add_6 (.a(dipswitch_1_out[3]), .b(dipswitch_9_out[3]), .c_i(add_5_c_o), .s(add_1_s[3]), .c_o(add_6_c_o));
  Add add_7 (.a(dipswitch_1_out[3]), .b(dipswitch_9_out[3]), .c_i(add_5_c_o), .s(add_1_s[3]), .c_o(add_6_c_o));
  Sub sub_5 (.a(dipswitch_1_out[3]), .b(dipswitch_9_out[3]), .c_i(sub_4_c_o), .s(sub_1_s[3]), .c_o(sub_5_c_o));
  Add add_8 (.a(dipswitch_1_out[2]), .b(dipswitch_9_out[2]), .c_i(add_6_c_o), .s(add_1_s[2]), .c_o(add_8_c_o));
  Sub sub_6 (.a(dipswitch_1_out[2]), .b(dipswitch_9_out[2]), .c_i(sub_5_c_o), .s(sub_1_s[2]), .c_o(sub_6_c_o));
  Add add_9 (.a(dipswitch_1_out[1]), .b(dipswitch_9_out[1]), .c_i(add_8_c_o), .s(add_1_s[1]), .c_o(add_9_c_o));
  Sub sub_7 (.a(dipswitch_1_out[1]), .b(dipswitch_9_out[1]), .c_i(sub_6_c_o), .s(sub_1_s[1]), .c_o(sub_7_c_o));
  Add add_10 (.a(dipswitch_1_out[0]), .b(dipswitch_9_out[0]), .c_i(add_9_c_o), .s(add_1_s[0]));  // open: c_o
  Sub sub_8 (.a(dipswitch_1_out[0]), .b(dipswitch_9_out[0]), .c_i(sub_7_c_o), .s(sub_1_s[0]));  // open: c_o
  Multiplexer #(.Bits(8)) multiplexer_1 (
    .sel(Addition___Subjection_out), .in_0(add_1_s), .in_1(sub_1_s), .out(multiplexer_1_out));
  DipSwitch dipswitch_1 (.out(dipswitch_1_out[7]));
  DipSwitch dipswitch_2 (.out(dipswitch_1_out[6]));
  LED led_1 (.in(multiplexer_1_out[7]));
  LED led_2 (.in(multiplexer_1_out[6]));
  DipSwitch dipswitch_3 (.out(dipswitch_1_out[5]));
  DipSwitch dipswitch_4 (.out(dipswitch_1_out[4]));
  LED led_3 (.in(multiplexer_1_out[5]));
  LED led_4 (.in(multiplexer_1_out[4]));
  DipSwitch dipswitch_5 (.out(dipswitch_1_out[3]));
  DipSwitch dipswitch_6 (.out(dipswitch_1_out[2]));
  LED led_5 (.in(multiplexer_1_out[3]));
  LED led_6 (.in(multiplexer_1_out[2]));
  DipSwitch dipswitch_7 (.out(dipswitch_1_out[1]));
  DipSwitch dipswitch_8 (.out(dipswitch_1_out[0]));
  LED led_7 (.in(multiplexer_1_out[1]));
  LED led_8 (.in(multiplexer_1_out[0]));
  DipSwitch dipswitch_9 (.out(dipswitch_9_out[7]));
  DipSwitch Addition___Subjection (.out(Addition___Subjection_out));
  DipSwitch dipswitch_10 (.out(dipswitch_9_out[6]));
  DipSwitch dipswitch_11 (.out(dipswitch_9_out[5]));
  DipSwitch dipswitch_12 (.out(dipswitch_9_out[4]));
  DipSwitch dipswitch_13 (.out(dipswitch_9_out[3]));
  DipSwitch dipswitch_14 (.out(dipswitch_9_out[2]));
  DipSwitch dipswitch_15 (.out(dipswitch_9_out[1]));
  DipSwitch dipswitch_16 (.out(dipswitch_9_out[0]));

  // Notes on the sheet:
  //   First number
  //   Second number
endmodule
