// Digital circuit Complex 8 bit ALU.dig as structural Verilog
module Complex_8_bit_ALU (
);

  wire and_1_out, and_2_out, and_3_out, and_4_out, and_5_out, and_6_out, and_7_out, and_8_out, and_9_out,
       and_10_out, and_11_out, and_12_out, and_13_out, and_14_out, and_15_out, and_16_out, and_17_out,
       and_18_out, and_19_out, and_20_out, and_21_out, and_22_out, and_23_out, and_24_out, and_25_out,
       and_26_out, and_27_out, and_28_out, and_29_out, and_30_out, and_31_out, and_32_out, and_33_out,
       and_34_out, and_35_out, and_36_out, and_37_out, and_38_out, and_39_out, and_40_out, and_41_out,
       and_42_out, and_43_out, and_44_out, and_45_out, and_46_out, and_47_out, and_48_out, and_49_out,
       and_50_out, and_51_out, and_52_out, and_53_out, and_54_out, and_55_out, and_56_out, and_57_out,
       and_58_out, and_59_out, and_60_out, and_61_out, and_62_out, and_63_out, and_64_out, and_65_out,
       and_66_out, and_67_out, and_68_out, and_69_out, and_70_out, and_71_out, and_72_out, and_73_out,
       and_74_out, and_75_out, and_76_out, and_77_out, and_78_out, and_79_out, and_80_out, and_81_out,
       and_82_out, and_83_out, and_84_out, and_85_out, and_86_out, and_87_out, and_88_out, and_89_out,
       and_90_out, and_91_out, and_92_out, and_93_out, and_94_out, and_95_out, and_96_out, and_97_out,
       and_98_out, and_99_out, and_100_out, and_101_out, and_102_out, and_103_out, and_104_out, button_1_out,
       dipswitch_1_out, dipswitch_2_out, dipswitch_3_out, dipswitch_4_out, dipswitch_5_out, dipswitch_6_out,
       dipswitch_7_out, dipswitch_8_out, dipswitch_9_out, dipswitch_10_out, dipswitch_11_out,
       dipswitch_12_out, dipswitch_13_out, dipswitch_14_out, dipswitch_15_out, dipswitch_16_out,
       dipswitch_17_out, dipswitch_18_out, dipswitch_19_out, not_1_out, not_2_out, not_3_out, not_4_out,
       not_5_out, not_6_out, not_7_out, not_8_out, not_9_out, not_10_out, not_11_out, not_12_out, not_13_out,
       not_14_out, not_15_out, not_16_out, not_17_out, not_18_out, not_19_out, not_20_out, not_21_out,
       not_22_out, not_23_out, not_24_out, not_25_out, not_26_out, not_27_out, not_28_out, not_29_out,
       not_30_out, not_31_out, not_32_out, not_33_out, not_34_out, not_35_out, not_36_out, not_37_out,
       not_38_out, not_39_out, not_40_out, not_41_out, not_42_out, not_43_out, not_44_out, not_45_out,
       not_46_out, not_47_out, not_48_out, or_1_out, or_2_out, or_3_out, or_4_out, or_5_out, or_6_out,
       or_7_out, or_8_out, or_9_out, or_10_out, or_11_out, or_12_out, or_13_out, or_14_out, or_15_out,
       or_16_out, or_17_out, or_18_out, or_19_out, or_20_out, or_21_out, or_22_out, or_23_out, or_24_out,
       or_25_out, or_26_out, or_27_out, or_28_out, or_29_out, or_30_out, or_31_out, or_32_out, or_33_out,
       or_34_out, or_35_out, or_36_out, or_37_out, or_38_out, or_39_out, or_40_out, or_41_out, or_42_out,
       or_43_out, or_44_out, or_45_out, or_46_out, or_47_out, or_48_out, or_49_out, or_50_out, or_51_out,
       or_52_out, or_53_out, or_54_out, or_55_out, or_56_out, xor_1_out, xor_2_out, xor_3_out, xor_4_out,
       xor_5_out, xor_6_out, xor_7_out, xor_8_out, xor_9_out, xor_10_out, xor_11_out, xor_12_out, xor_13_out,
       xor_14_out, xor_15_out, xor_16_out, xor_17_out, xor_18_out, xor_19_out, xor_20_out, xor_21_out,
       xor_22_out, xor_23_out, xor_24_out, xor_25_out, xor_26_out, xor_27_out, xor_28_out, xor_29_out,
       xor_30_out, xor_31_out, xor_32_out, xor_33_out, xor_34_out, xor_35_out, xor_36_out, xor_37_out,
       xor_38_out, xor_39_out, xor_40_out;

  and and_1 (and_1_out, dipswitch_19_out, dipswitch_11_out);
  and and_2 (and_2_out, dipswitch_18_out, dipswitch_10_out);
  and and_3 (and_3_out, dipswitch_17_out, dipswitch_9_out);
  and and_4 (and_4_out, dipswitch_16_out, dipswitch_8_out);
  and and_5 (and_5_out, dipswitch_15_out, dipswitch_7_out);
  and and_6 (and_6_out, dipswitch_14_out, dipswitch_6_out);
  and and_7 (and_7_out, dipswitch_13_out, dipswitch_5_out);
  and and_8 (and_8_out, dipswitch_12_out, dipswitch_1_out);
  or or_1 (or_1_out, dipswitch_19_out, dipswitch_11_out);
  or or_2 (or_2_out, dipswitch_18_out, dipswitch_10_out);
  or or_3 (or_3_out, dipswitch_17_out, dipswitch_9_out);
  or or_4 (or_4_out, dipswitch_16_out, dipswitch_8_out);
  or or_5 (or_5_out, dipswitch_15_out, dipswitch_7_out);
  or or_6 (or_6_out, dipswitch_14_out, dipswitch_6_out);
  or or_7 (or_7_out, dipswitch_13_out, dipswitch_5_out);
  or or_8 (or_8_out, dipswitch_12_out, dipswitch_1_out);
  xor xor_1 (xor_1_out, dipswitch_19_out, dipswitch_11_out);
  xor xor_2 (xor_2_out, dipswitch_18_out, dipswitch_10_out);
  xor xor_3 (xor_3_out, dipswitch_17_out, dipswitch_9_out);
  xor xor_4 (xor_4_out, dipswitch_16_out, dipswitch_8_out);
  xor xor_5 (xor_5_out, dipswitch_15_out, dipswitch_7_out);
  xor xor_6 (xor_6_out, dipswitch_14_out, dipswitch_6_out);
  xor xor_7 (xor_7_out, dipswitch_13_out, dipswitch_5_out);
  xor xor_8 (xor_8_out, dipswitch_12_out, dipswitch_1_out);
  Button button_1 (.out(button_1_out));
  xor xor_9 (xor_9_out, dipswitch_11_out, dipswitch_12_out);
  xor xor_10 (xor_10_out, dipswitch_10_out, dipswitch_18_out);
  xor xor_11 (xor_11_out, dipswitch_9_out, dipswitch_17_out);
  xor xor_12 (xor_12_out, dipswitch_8_out, dipswitch_16_out);
  xor xor_13 (xor_13_out, dipswitch_7_out, dipswitch_15_out);
  xor xor_14 (xor_14_out, dipswitch_6_out, dipswitch_14_out);
  xor xor_15 (xor_15_out, dipswitch_5_out, dipswitch_13_out);
  xor xor_16 (xor_16_out, dipswitch_1_out, dipswitch_12_out);
  xor xor_17 (xor_17_out, dipswitch_11_out, dipswitch_19_out);
  not not_1 (not_1_out, dipswitch_11_out);
  xor xor_18 (xor_18_out, dipswitch_10_out, dipswitch_18_out);
  not not_2 (not_2_out, dipswitch_10_out);
  xor xor_19 (xor_19_out, dipswitch_9_out, dipswitch_17_out);
  not not_3 (not_3_out, dipswitch_9_out);
  xor xor_20 (xor_20_out, dipswitch_8_out, dipswitch_16_out);
  not not_4 (not_4_out, dipswitch_8_out);
  xor xor_21 (xor_21_out, dipswitch_7_out, dipswitch_15_out);
  not not_5 (not_5_out, dipswitch_7_out);
  xor xor_22 (xor_22_out, dipswitch_6_out, dipswitch_14_out);
  not not_6 (not_6_out, dipswitch_6_out);
  xor xor_23 (xor_23_out, dipswitch_5_out, dipswitch_13_out);
  not not_7 (not_7_out, dipswitch_5_out);
  xor xor_24 (xor_24_out, dipswitch_1_out, dipswitch_12_out);
  not not_8 (not_8_out, dipswitch_1_out);
  not not_9 (not_9_out, xor_17_out);
  not not_10 (not_10_out, xor_18_out);
  not not_11 (not_11_out, xor_19_out);
  not not_12 (not_12_out, xor_20_out);
  not not_13 (not_13_out, xor_21_out);
  not not_14 (not_14_out, xor_22_out);
  not not_15 (not_15_out, xor_23_out);
  not not_16 (not_16_out, xor_24_out);
  xor xor_25 (xor_25_out, xor_9_out, dipswitch_19_out);
  and and_9 (and_9_out, dipswitch_19_out, xor_9_out);
  and and_10 (and_10_out, dipswitch_12_out, dipswitch_11_out);
  xor xor_26 (xor_26_out, xor_10_out, or_9_out);
  and and_11 (and_11_out, or_9_out, xor_10_out);
  and and_12 (and_12_out, dipswitch_18_out, dipswitch_10_out);
  xor xor_27 (xor_27_out, xor_11_out, or_10_out);
  and and_13 (and_13_out, or_10_out, xor_11_out);
  and and_14 (and_14_out, dipswitch_17_out, dipswitch_9_out);
  xor xor_28 (xor_28_out, xor_12_out, or_11_out);
  and and_15 (and_15_out, or_11_out, xor_12_out);
  and and_16 (and_16_out, dipswitch_16_out, dipswitch_8_out);
  xor xor_29 (xor_29_out, xor_13_out, or_12_out);
  and and_17 (and_17_out, or_12_out, xor_13_out);
  and and_18 (and_18_out, dipswitch_15_out, dipswitch_7_out);
  xor xor_30 (xor_30_out, xor_14_out, or_13_out);
  and and_19 (and_19_out, or_13_out, xor_14_out);
  and and_20 (and_20_out, dipswitch_14_out, dipswitch_6_out);
  xor xor_31 (xor_31_out, xor_15_out, or_14_out);
  and and_21 (and_21_out, or_14_out, xor_15_out);
  and and_22 (and_22_out, dipswitch_13_out, dipswitch_5_out);
  xor xor_32 (xor_32_out, xor_16_out, or_15_out);
  and and_23 (and_23_out, or_15_out, xor_16_out);
  and and_24 (and_24_out, dipswitch_12_out, dipswitch_1_out);
  xor xor_33 (xor_33_out, xor_17_out, button_1_out);
  and and_25 (and_25_out, button_1_out, not_9_out);
  and and_26 (and_26_out, dipswitch_19_out, not_1_out);
  xor xor_34 (xor_34_out, xor_18_out, or_17_out);
  and and_27 (and_27_out, or_17_out, not_10_out);
  and and_28 (and_28_out, dipswitch_18_out, not_2_out);
  xor xor_35 (xor_35_out, xor_19_out, or_18_out);
  and and_29 (and_29_out, or_18_out, not_11_out);
  and and_30 (and_30_out, dipswitch_17_out, not_3_out);
  xor xor_36 (xor_36_out, xor_20_out, or_19_out);
  and and_31 (and_31_out, or_19_out, not_12_out);
  and and_32 (and_32_out, dipswitch_16_out, not_4_out);
  xor xor_37 (xor_37_out, xor_21_out, or_20_out);
  and and_33 (and_33_out, or_20_out, not_13_out);
  and and_34 (and_34_out, dipswitch_15_out, not_5_out);
  xor xor_38 (xor_38_out, xor_22_out, or_21_out);
  and and_35 (and_35_out, or_21_out, not_14_out);
  and and_36 (and_36_out, dipswitch_14_out, not_6_out);
  xor xor_39 (xor_39_out, xor_23_out, or_22_out);
  and and_37 (and_37_out, or_22_out, not_15_out);
  and and_38 (and_38_out, dipswitch_13_out, not_7_out);
  xor xor_40 (xor_40_out, xor_24_out, or_23_out);
  and and_39 (and_39_out, or_23_out, not_16_out);
  and and_40 (and_40_out, dipswitch_12_out, not_8_out);
  or or_9 (or_9_out, and_9_out, and_10_out);
  or or_10 (or_10_out, and_11_out, and_12_out);
  or or_11 (or_11_out, and_13_out, and_14_out);
  or or_12 (or_12_out, and_15_out, and_16_out);
  or or_13 (or_13_out, and_17_out, and_18_out);
  or or_14 (or_14_out, and_19_out, and_20_out);
  or or_15 (or_15_out, and_21_out, and_22_out);
  or or_16 (or_16_out, and_23_out, and_24_out);
  or or_17 (or_17_out, and_25_out, and_26_out);
  or or_18 (or_18_out, and_27_out, and_28_out);
  or or_19 (or_19_out, and_29_out, and_30_out);
  or or_20 (or_20_out, and_31_out, and_32_out);
  or or_21 (or_21_out, and_33_out, and_34_out);
  or or_22 (or_22_out, and_35_out, and_36_out);
  or or_23 (or_23_out, and_37_out, and_38_out);
  or or_24 (or_24_out, and_39_out, and_40_out);
  and and_41 (and_41_out, xor_25_out, not_17_out);
  not not_17 (not_17_out, dipswitch_4_out);
  and and_42 (and_42_out, dipswitch_4_out, xor_33_out);
  and and_43 (and_43_out, xor_26_out, not_18_out);
  not not_18 (not_18_out, dipswitch_4_out);
  and and_44 (and_44_out, dipswitch_4_out, xor_34_out);
  and and_45 (and_45_out, xor_27_out, not_19_out);
  not not_19 (not_19_out, dipswitch_4_out);
  and and_46 (and_46_out, dipswitch_4_out, xor_35_out);
  and and_47 (and_47_out, xor_28_out, not_20_out);
  not not_20 (not_20_out, dipswitch_4_out);
  and and_48 (and_48_out, dipswitch_4_out, xor_36_out);
  and and_49 (and_49_out, xor_29_out, not_21_out);
  not not_21 (not_21_out, dipswitch_4_out);
  and and_50 (and_50_out, dipswitch_4_out, xor_37_out);
  and and_51 (and_51_out, xor_30_out, not_22_out);
  not not_22 (not_22_out, dipswitch_4_out);
  and and_52 (and_52_out, dipswitch_4_out, xor_38_out);
  and and_53 (and_53_out, xor_31_out, not_23_out);
  not not_23 (not_23_out, dipswitch_4_out);
  and and_54 (and_54_out, dipswitch_4_out, xor_39_out);
  and and_55 (and_55_out, xor_32_out, not_24_out);
  not not_24 (not_24_out, dipswitch_4_out);
  and and_56 (and_56_out, dipswitch_4_out, xor_40_out);
  and and_57 (and_57_out, xor_8_out, not_25_out);
  not not_25 (not_25_out, dipswitch_4_out);
  and and_58 (and_58_out, dipswitch_4_out, or_8_out);
  and and_59 (and_59_out, xor_7_out, not_26_out);
  not not_26 (not_26_out, dipswitch_4_out);
  and and_60 (and_60_out, dipswitch_4_out, or_7_out);
  and and_61 (and_61_out, xor_6_out, not_27_out);
  not not_27 (not_27_out, dipswitch_4_out);
  and and_62 (and_62_out, dipswitch_4_out, or_6_out);
  and and_63 (and_63_out, xor_5_out, not_28_out);
  not not_28 (not_28_out, dipswitch_4_out);
  and and_64 (and_64_out, dipswitch_4_out, or_5_out);
  and and_65 (and_65_out, xor_4_out, not_29_out);
  not not_29 (not_29_out, dipswitch_4_out);
  and and_66 (and_66_out, dipswitch_4_out, or_4_out);
  and and_67 (and_67_out, xor_3_out, not_30_out);
  not not_30 (not_30_out, dipswitch_4_out);
  and and_68 (and_68_out, dipswitch_4_out, or_3_out);
  and and_69 (and_69_out, xor_2_out, not_31_out);
  not not_31 (not_31_out, dipswitch_4_out);
  and and_70 (and_70_out, dipswitch_4_out, or_2_out);
  and and_71 (and_71_out, xor_1_out, not_32_out);
  not not_32 (not_32_out, dipswitch_4_out);
  and and_72 (and_72_out, dipswitch_4_out, or_1_out);
  or or_25 (or_25_out, and_41_out, and_42_out);
  or or_26 (or_26_out, and_43_out, and_44_out);
  or or_27 (or_27_out, and_45_out, and_46_out);
  or or_28 (or_28_out, and_47_out, and_48_out);
  or or_29 (or_29_out, and_49_out, and_50_out);
  or or_30 (or_30_out, and_51_out, and_52_out);
  or or_31 (or_31_out, and_53_out, and_54_out);
  or or_32 (or_32_out, and_55_out, and_56_out);
  or or_33 (or_33_out, and_57_out, and_58_out);
  or or_34 (or_34_out, and_59_out, and_60_out);
  or or_35 (or_35_out, and_61_out, and_62_out);
  or or_36 (or_36_out, and_63_out, and_64_out);
  or or_37 (or_37_out, and_65_out, and_66_out);
  or or_38 (or_38_out, and_67_out, and_68_out);
  or or_39 (or_39_out, and_69_out, and_70_out);
  or or_40 (or_40_out, and_71_out, and_72_out);
  not not_33 (not_33_out, dipswitch_3_out);
  not not_34 (not_34_out, dipswitch_3_out);
  not not_35 (not_35_out, dipswitch_3_out);
  not not_36 (not_36_out, dipswitch_3_out);
  not not_37 (not_37_out, dipswitch_3_out);
  not not_38 (not_38_out, dipswitch_3_out);
  not not_39 (not_39_out, dipswitch_3_out);
  not not_40 (not_40_out, dipswitch_3_out);
  and and_73 (and_73_out, or_32_out, not_33_out);
  and and_74 (and_74_out, dipswitch_3_out, or_33_out);
  and and_75 (and_75_out, or_31_out, not_34_out);
  and and_76 (and_76_out, dipswitch_3_out, or_34_out);
  and and_77 (and_77_out, or_30_out, not_35_out);
  and and_78 (and_78_out, dipswitch_3_out, or_35_out);
  and and_79 (and_79_out, or_29_out, not_36_out);
  and and_80 (and_80_out, dipswitch_3_out, or_36_out);
  and and_81 (and_81_out, or_28_out, not_37_out);
  and and_82 (and_82_out, dipswitch_3_out, or_37_out);
  and and_83 (and_83_out, or_27_out, not_38_out);
  and and_84 (and_84_out, dipswitch_3_out, or_38_out);
  and and_85 (and_85_out, or_26_out, not_39_out);
  and and_86 (and_86_out, dipswitch_3_out, or_39_out);
  and and_87 (and_87_out, or_25_out, not_40_out);
  and and_88 (and_88_out, dipswitch_3_out, or_40_out);
  or or_41 (or_41_out, and_73_out, and_74_out);
  or or_42 (or_42_out, and_75_out, and_76_out);
  or or_43 (or_43_out, and_77_out, and_78_out);
  or or_44 (or_44_out, and_79_out, and_80_out);
  or or_45 (or_45_out, and_81_out, and_82_out);
  or or_46 (or_46_out, and_83_out, and_84_out);
  or or_47 (or_47_out, and_85_out, and_86_out);
  or or_48 (or_48_out, and_87_out, and_88_out);
  not not_41 (not_41_out, dipswitch_2_out);
  not not_42 (not_42_out, dipswitch_2_out);
  not not_43 (not_43_out, dipswitch_2_out);
  not not_44 (not_44_out, dipswitch_2_out);
  not not_45 (not_45_out, dipswitch_2_out);
  not not_46 (not_46_out, dipswitch_2_out);
  not not_47 (not_47_out, dipswitch_2_out);
  not not_48 (not_48_out, dipswitch_2_out);
  and and_89 (and_89_out, or_41_out, not_41_out);
  and and_90 (and_90_out, dipswitch_2_out, and_8_out);
  and and_91 (and_91_out, or_42_out, not_42_out);
  and and_92 (and_92_out, dipswitch_2_out, and_7_out);
  and and_93 (and_93_out, or_43_out, not_43_out);
  and and_94 (and_94_out, dipswitch_2_out, and_6_out);
  and and_95 (and_95_out, or_44_out, not_44_out);
  and and_96 (and_96_out, dipswitch_2_out, and_5_out);
  and and_97 (and_97_out, or_45_out, not_45_out);
  and and_98 (and_98_out, dipswitch_2_out, and_4_out);
  and and_99 (and_99_out, or_46_out, not_46_out);
  and and_100 (and_100_out, dipswitch_2_out, and_3_out);
  and and_101 (and_101_out, or_47_out, not_47_out);
  and and_102 (and_102_out, dipswitch_2_out, and_2_out);
  and and_103 (and_103_out, or_48_out, not_48_out);
  and and_104 (and_104_out, dipswitch_2_out, and_1_out);
  or or_49 (or_49_out, and_89_out, and_90_out);
  or or_50 (or_50_out, and_91_out, and_92_out);
  or or_51 (or_51_out, and_93_out, and_94_out);
  or or_52 (or_52_out, and_95_out, and_96_out);
  or or_53 (or_53_out, and_97_out, and_98_out);
  or or_54 (or_54_out, and_99_out, and_100_out);
  or or_55 (or_55_out, and_101_out, and_102_out);
  or or_56 (or_56_out, and_103_out, and_104_out);
  LED led_1 (.in(or_49_out));
  LED led_2 (.in(or_50_out));
  LED led_3 (.in(or_51_out));
  LED led_4 (.in(or_52_out));
  LED led_5 (.in(or_53_out));
  LED led_6 (.in(or_54_out));
  LED led_7 (.in(or_55_out));
  LED led_8 (.in(or_56_out));
  DipSwitch dipswitch_1 (.out(dipswitch_1_out));
  DipSwitch dipswitch_2 (.out(dipswitch_2_out));
  DipSwitch dipswitch_3 (.out(dipswitch_3_out));
  DipSwitch dipswitch_4 (.out(dipswitch_4_out));
  DipSwitch dipswitch_5 (.out(dipswitch_5_out));
  DipSwitch dipswitch_6 (.out(dipswitch_6_out));
  DipSwitch dipswitch_7 (.out(dipswitch_7_out));
  DipSwitch dipswitch_8 (.out(dipswitch_8_out));
  DipSwitch dipswitch_9 (.out(dipswitch_9_out));
  DipSwitch dipswitch_10 (.out(dipswitch_10_out));
  DipSwitch dipswitch_11 (.out(dipswitch_11_out));
  DipSwitch dipswitch_12 (.out(dipswitch_12_out));
  DipSwitch dipswitch_13 (.out(dipswitch_13_out));
  DipSwitch dipswitch_14 (.out(dipswitch_14_out));
  DipSwitch dipswitch_15 (.out(dipswitch_15_out));
  DipSwitch dipswitch_16 (.out(dipswitch_16_out));
  DipSwitch dipswitch_17 (.out(dipswitch_17_out));
  DipSwitch dipswitch_18 (.out(dipswitch_18_out));
  DipSwitch dipswitch_19 (.out(dipswitch_19_out));

  // Notes on the sheet:
  //   000 - Addition
  //   001 - Subtraction
  //   010 - A XOR B
  //   011 - A OR B
  //   100 - A AND B
endmodule
