// Digital circuit Full adder.dig as structural Verilog
module Full_adder (
);

  wire and_1_out, and_2_out, or_1_out, undriven, undriven_2, undriven_3, xor_1_out, xor_2_out;

  xor xor_1 (xor_1_out, undriven, undriven_2);
  xor xor_2 (xor_2_out, xor_1_out, undriven_3);
  and and_1 (and_1_out, undriven_3, xor_1_out);
  and and_2 (and_2_out, undriven_2, undriven);
  or or_1 (or_1_out, and_1_out, and_2_out);

  // Notes on the sheet:
  //   A
  //   B
  //   C
  //   in
  //   Sum
  //   out
endmodule
