// Digital circuit Half adder.dig as structural Verilog
module Half_adder (
);

  wire and_1_out, undriven, undriven_2, xor_1_out;

  xor xor_1 (xor_1_out, undriven, undriven_2);
  and and_1 (and_1_out, undriven_2, undriven);

  // Notes on the sheet:
  //   A
  //   B
  //   Sum
  //   C
  //   out
endmodule
