// Digital circuit Half subtractor.dig as structural Verilog
module Half_subtractor (
);

  wire and_1_out, not_1_out, undriven, undriven_2, xor_1_out;

  xor xor_1 (xor_1_out, undriven, undriven_2);
  not not_1 (not_1_out, undriven);
  and and_1 (and_1_out, undriven_2, not_1_out);

  // Notes on the sheet:
  //   A
  //   B
  //   Difference
  //   C
  //   out
endmodule
