// Digital circuit 4 bit CPU.dig as structural Verilog
module _4_bit_CPU (
);

  wire and_1_out, and_2_out, and_3_out, and_4_out, and_5_out, and_6_out, and_7_out, and_8_out, and_9_out,
       and_10_out, and_11_out, and_12_out, and_13_out, and_14_out, and_15_out, and_16_out, and_17_out,
       and_18_out, and_19_out, and_20_out, and_21_out, and_22_out, and_23_out, and_24_out, and_25_out,
       and_26_out, and_27_out, and_28_out, and_29_out, and_30_out, and_31_out, and_32_out, and_33_out,
       and_34_out, and_35_out, and_36_out, and_37_out, and_38_out, and_39_out, and_40_out, and_41_out,
       and_42_out, and_43_out, and_44_out, and_45_out, and_46_out, and_47_out, and_48_out, and_49_out,
       and_50_out, and_51_out, and_52_out, and_53_out, and_54_out, and_55_out, and_56_out, and_57_out,
       and_58_out, and_59_out, and_60_out, and_61_out, and_62_out, and_63_out, and_64_out, and_65_out,
       and_66_out, and_67_out, and_68_out, and_69_out, and_70_out, and_71_out, and_72_out, and_73_out,
       and_74_out, and_75_out, and_76_out, and_77_out, and_78_out, and_79_out, and_80_out, and_81_out,
       and_82_out, and_83_out, and_84_out, and_85_out, and_86_out, and_87_out, and_88_out, and_89_out,
       and_90_out, and_91_out, and_92_out, and_93_out, and_94_out, and_95_out, and_96_out, and_97_out,
       and_98_out, and_99_out, and_100_out, and_101_out, and_102_out, and_103_out, and_104_out, and_105_out,
       and_106_out, and_107_out, and_108_out, and_109_out, and_110_out, and_111_out, and_112_out,
       and_113_out, and_114_out, and_115_out, and_116_out, and_117_out, and_118_out, and_119_out,
       and_120_out, and_121_out, and_122_out, and_123_out, and_124_out, and_125_out, and_126_out,
       and_127_out, and_128_out, and_129_out, and_130_out, and_131_out, and_132_out, and_133_out,
       and_134_out, and_135_out, and_136_out, and_137_out, and_138_out, and_139_out, and_140_out,
       and_141_out, and_142_out, and_143_out, and_144_out, and_145_out, and_146_out, and_147_out,
       and_148_out, and_149_out, and_150_out, and_151_out, and_152_out, and_153_out, and_154_out,
       and_155_out, and_156_out, and_157_out, and_158_out, and_159_out, and_160_out, and_161_out,
       and_162_out, and_163_out, and_164_out, and_165_out, and_166_out, and_167_out, and_168_out,
       and_169_out, and_170_out, and_171_out, and_172_out, and_173_out, and_174_out, and_175_out,
       and_176_out, and_177_out, and_178_out, and_179_out, and_180_out, and_181_out, and_182_out,
       and_183_out, and_184_out, and_185_out, and_186_out, and_187_out, and_188_out, and_189_out,
       and_190_out, and_191_out, and_192_out, and_193_out, and_194_out, and_195_out, and_196_out,
       and_197_out, and_205_out, and_206_out, and_207_out, and_208_out, and_209_out, and_210_out,
       and_211_out, and_212_out, and_213_out, and_214_out, and_215_out, and_216_out, and_217_out,
       and_218_out, and_219_out, and_220_out, and_221_out, and_222_out, and_223_out, and_224_out,
       and_225_out, and_226_out, and_227_out, and_228_out, and_229_out, and_230_out, and_231_out,
       and_232_out, and_233_out, and_234_out, and_235_out, and_236_out, and_237_out, and_238_out,
       and_239_out, and_240_out, and_241_out, and_242_out, and_243_out, and_244_out, and_245_out,
       and_253_out, and_254_out, and_255_out, and_256_out, and_257_out, and_258_out, and_259_out,
       and_260_out, and_261_out, and_262_out, and_263_out, and_264_out, and_265_out, and_266_out,
       and_267_out, and_268_out, and_269_out, and_270_out, and_271_out, and_272_out, and_273_out,
       and_274_out, and_275_out, and_276_out, and_277_out, and_278_out, and_279_out, and_280_out,
       and_281_out, and_282_out, and_283_out, and_284_out, and_285_out, and_286_out, and_287_out,
       and_288_out, and_289_out, and_290_out, and_291_out, and_292_out, and_293_out, and_301_out,
       and_302_out, and_303_out, and_304_out, and_305_out, and_306_out, and_307_out, and_308_out,
       and_309_out, and_310_out, and_311_out, and_312_out, and_313_out, and_314_out, and_315_out,
       and_316_out, and_317_out, and_318_out, and_319_out, and_320_out, and_321_out, and_322_out,
       and_323_out, and_324_out, and_325_out, and_326_out, and_327_out, and_328_out, and_329_out,
       and_330_out, and_331_out, and_332_out, and_333_out, and_334_out, and_335_out, and_336_out,
       and_337_out, and_338_out, and_339_out, and_340_out, and_341_out, nand_1_out, nand_2_out, nand_3_out,
       nand_4_out, nand_5_out, nand_6_out, nand_7_out, nand_8_out, nand_9_out, nand_10_out, nand_11_out,
       nand_12_out, nand_13_out, nand_14_out, nand_15_out, nand_16_out, nand_17_out, nand_18_out,
       nand_19_out, nand_20_out, nor_1_out, nor_2_out, nor_3_out, nor_4_out, nor_5_out, nor_6_out, nor_7_out,
       nor_8_out, nor_9_out, nor_10_out, nor_11_out, nor_12_out, nor_13_out, nor_14_out, nor_15_out,
       nor_16_out, nor_17_out, nor_18_out, nor_19_out, nor_20_out, nor_21_out, nor_22_out, nor_23_out,
       nor_24_out, nor_25_out, nor_26_out, nor_27_out, nor_28_out, nor_29_out, nor_30_out, nor_31_out,
       nor_32_out, nor_33_out, nor_34_out, nor_35_out, nor_36_out, nor_37_out, nor_38_out, nor_39_out,
       nor_40_out, nor_41_out, nor_42_out, nor_43_out, nor_44_out, nor_45_out, nor_46_out, nor_47_out,
       nor_48_out, nor_49_out, nor_50_out, nor_51_out, nor_52_out, nor_53_out, nor_54_out, nor_55_out,
       nor_56_out, nor_57_out, nor_58_out, nor_59_out, nor_60_out, nor_61_out, nor_62_out, nor_63_out,
       nor_64_out, nor_65_out, nor_66_out, nor_67_out, nor_68_out, not_1_out, not_2_out, not_3_out,
       not_4_out, not_5_out, not_6_out, not_7_out, not_8_out, not_9_out, not_10_out, not_11_out, not_12_out,
       not_13_out, not_14_out, not_15_out, not_16_out, not_17_out, not_18_out, not_19_out, not_20_out,
       not_21_out, not_22_out, not_23_out, not_24_out, not_25_out, not_26_out, not_27_out, not_28_out,
       not_29_out, not_30_out, not_31_out, not_32_out, not_33_out, not_34_out, not_35_out, not_36_out,
       not_37_out, not_38_out, not_39_out, not_40_out, not_41_out, not_42_out, not_43_out, not_44_out,
       not_45_out, not_46_out, not_47_out, not_48_out, not_49_out, not_50_out, not_51_out, not_52_out,
       not_53_out, not_54_out, not_55_out, not_56_out, not_57_out, not_58_out, not_59_out, not_60_out,
       not_61_out, not_62_out, not_63_out, not_64_out, not_65_out, not_66_out, not_67_out, not_68_out,
       not_69_out, not_70_out, not_71_out, not_72_out, not_73_out, not_74_out, not_75_out, not_76_out,
       not_77_out, not_78_out, not_79_out, not_80_out, not_81_out, not_82_out, not_83_out, not_84_out,
       not_85_out, not_86_out, not_87_out, not_88_out, not_89_out, not_90_out, not_91_out, not_92_out,
       not_93_out, not_94_out, not_95_out, not_96_out, or_1_out, or_2_out, or_3_out, or_4_out, or_5_out,
       or_6_out, or_7_out, or_9_out, or_10_out, or_11_out, or_13_out, or_14_out, or_15_out, or_16_out,
       or_17_out, or_18_out, or_19_out, or_20_out, or_21_out, or_22_out, or_23_out, or_24_out, or_25_out,
       or_26_out, or_27_out, or_28_out, or_29_out, or_30_out, or_31_out, or_32_out, or_33_out, or_34_out,
       or_35_out, or_36_out, or_37_out, or_38_out, or_39_out, or_40_out, or_41_out, or_42_out, or_43_out,
       or_44_out, or_45_out, or_46_out, or_47_out, or_48_out, or_49_out, undriven, undriven_2, undriven_3,
       undriven_4, undriven_5, undriven_6, undriven_7, undriven_8, undriven_9, undriven_10, undriven_11,
       undriven_12, undriven_13, undriven_14, undriven_15, undriven_16, undriven_17, undriven_18,
       undriven_19, undriven_20, undriven_21, undriven_22, undriven_23, undriven_24, undriven_25,
       undriven_26, undriven_27, undriven_28, undriven_29, undriven_30, undriven_31, xnor_1_out, xnor_2_out,
       xnor_3_out, xnor_4_out, xor_1_out, xor_2_out, xor_3_out, xor_4_out, xor_5_out, xor_6_out, xor_7_out,
       xor_8_out, xor_9_out, xor_10_out, xor_11_out, xor_12_out, xor_13_out, xor_14_out, xor_15_out,
       xor_16_out, xor_17_out, xor_18_out, xor_19_out, xor_20_out;

  and and_1 (and_1_out, undriven_4, undriven_8);
  and and_2 (and_2_out, undriven_3, undriven_7);
  and and_3 (and_3_out, undriven_2, undriven_6);
  and and_4 (and_4_out, undriven, undriven_5);
  nand nand_1 (nand_1_out, undriven_4, undriven_8);
  nand nand_2 (nand_2_out, undriven_3, undriven_7);
  nand nand_3 (nand_3_out, undriven_2, undriven_6);
  nand nand_4 (nand_4_out, undriven, undriven_5);
  or or_1 (or_1_out, undriven_4, undriven_8);
  or or_2 (or_2_out, undriven_3, undriven_7);
  or or_3 (or_3_out, undriven_2, undriven_6);
  or or_4 (or_4_out, undriven, undriven_5);
  xor xor_1 (xor_1_out, undriven_4, undriven_8);
  xor xor_2 (xor_2_out, undriven_3, undriven_7);
  xor xor_3 (xor_3_out, undriven_2, undriven_6);
  xor xor_4 (xor_4_out, undriven, undriven_5);
  nor nor_1 (nor_1_out, undriven_4, undriven_8);
  nor nor_2 (nor_2_out, undriven_3, undriven_7);
  nor nor_3 (nor_3_out, undriven_2, undriven_6);
  nor nor_4 (nor_4_out, undriven, undriven_5);
  xnor xnor_1 (xnor_1_out, undriven_4, undriven_8);
  xnor xnor_2 (xnor_2_out, undriven_3, undriven_7);
  xnor xnor_3 (xnor_3_out, undriven_2, undriven_6);
  xnor xnor_4 (xnor_4_out, undriven, undriven_5);
  xor xor_5 (xor_5_out, undriven_8, undriven_4);
  xor xor_6 (xor_6_out, undriven_7, undriven_3);
  xor xor_7 (xor_7_out, undriven_6, undriven_2);
  xor xor_8 (xor_8_out, undriven_5, undriven);
  xor xor_9 (xor_9_out, undriven_8, undriven_4);
  not not_1 (not_1_out, undriven_8);
  xor xor_10 (xor_10_out, undriven_7, undriven_3);
  not not_2 (not_2_out, undriven_7);
  xor xor_11 (xor_11_out, undriven_6, undriven_2);
  not not_3 (not_3_out, undriven_6);
  xor xor_12 (xor_12_out, undriven_5, undriven);
  not not_4 (not_4_out, undriven_5);
  xor xor_13 (xor_13_out, xor_5_out, undriven_9);
  and and_5 (and_5_out, undriven_9, xor_5_out);
  and and_6 (and_6_out, undriven_4, undriven_8);
  xor xor_14 (xor_14_out, xor_6_out, or_5_out);
  and and_7 (and_7_out, or_5_out, xor_6_out);
  and and_8 (and_8_out, undriven_3, undriven_7);
  xor xor_15 (xor_15_out, xor_7_out, or_6_out);
  and and_9 (and_9_out, or_6_out, xor_7_out);
  and and_10 (and_10_out, undriven_2, undriven_6);
  xor xor_16 (xor_16_out, xor_8_out, or_7_out);
  and and_11 (and_11_out, or_7_out, xor_8_out);
  and and_12 (and_12_out, undriven, undriven_5);
  xor xor_17 (xor_17_out, xor_9_out, undriven_10);
  not not_5 (not_5_out, xor_9_out);
  and and_13 (and_13_out, undriven_10, not_5_out);
  and and_14 (and_14_out, undriven_4, not_1_out);
  xor xor_18 (xor_18_out, xor_10_out, or_9_out);
  not not_6 (not_6_out, xor_10_out);
  and and_15 (and_15_out, or_9_out, not_6_out);
  and and_16 (and_16_out, undriven_3, not_2_out);
  xor xor_19 (xor_19_out, xor_11_out, or_10_out);
  not not_7 (not_7_out, xor_11_out);
  and and_17 (and_17_out, or_10_out, not_7_out);
  and and_18 (and_18_out, undriven_2, not_3_out);
  xor xor_20 (xor_20_out, xor_12_out, or_11_out);
  not not_8 (not_8_out, xor_12_out);
  and and_19 (and_19_out, or_11_out, not_8_out);
  and and_20 (and_20_out, undriven, not_4_out);
  or or_5 (or_5_out, and_5_out, and_6_out);
  or or_6 (or_6_out, and_7_out, and_8_out);
  or or_7 (or_7_out, and_9_out, and_10_out);
  // Or or_8 has open pins: In_1=and_11_out, In_2=and_12_out, out=open
  or or_9 (or_9_out, and_13_out, and_14_out);
  or or_10 (or_10_out, and_15_out, and_16_out);
  or or_11 (or_11_out, and_17_out, and_18_out);
  // Or or_12 has open pins: In_1=and_19_out, In_2=and_20_out, out=open
  not not_9 (not_9_out, or_15_out);
  not not_10 (not_10_out, undriven_11);
  not not_11 (not_11_out, undriven_12);
  not not_12 (not_12_out, undriven_13);
  not not_13 (not_13_out, undriven_14);
  not not_14 (not_14_out, undriven_15);
  not not_15 (not_15_out, undriven_16);
  not not_16 (not_16_out, undriven_17);
  or or_13 (or_13_out, and_132_out, and_130_out);
  or or_14 (or_14_out, and_128_out, and_126_out);
  or or_15 (or_15_out, or_13_out, or_14_out);
  not not_17 (not_17_out, or_17_out);
  not not_18 (not_18_out, undriven_18);
  not not_19 (not_19_out, undriven_19);
  not not_20 (not_20_out, undriven_20);
  not not_21 (not_21_out, undriven_21);
  not not_22 (not_22_out, undriven_22);
  not not_23 (not_23_out, undriven_23);
  not not_24 (not_24_out, undriven_24);
  or or_16 (or_16_out, and_128_out, and_127_out);
  or or_17 (or_17_out, or_18_out, or_16_out);
  and and_21 (and_21_out, not_17_out, xor_13_out);
  and and_22 (and_22_out, or_17_out, xor_17_out);
  and and_23 (and_23_out, or_15_out, and_1_out);
  and and_24 (and_24_out, or_15_out, nand_1_out);
  and and_25 (and_25_out, not_18_out, xor_14_out);
  and and_26 (and_26_out, undriven_18, xor_18_out);
  and and_27 (and_27_out, undriven_11, and_2_out);
  and and_28 (and_28_out, undriven_11, nand_2_out);
  and and_29 (and_29_out, not_19_out, xor_15_out);
  and and_30 (and_30_out, undriven_19, xor_19_out);
  and and_31 (and_31_out, undriven_12, and_3_out);
  and and_32 (and_32_out, undriven_12, nand_3_out);
  and and_33 (and_33_out, not_20_out, xor_16_out);
  and and_34 (and_34_out, undriven_20, xor_20_out);
  and and_35 (and_35_out, undriven_13, and_4_out);
  and and_36 (and_36_out, undriven_13, nand_4_out);
  and and_37 (and_37_out, not_21_out, xnor_1_out);
  and and_38 (and_38_out, undriven_21, nor_1_out);
  and and_39 (and_39_out, undriven_14, xor_1_out);
  and and_40 (and_40_out, undriven_14, or_1_out);
  and and_41 (and_41_out, not_22_out, xnor_2_out);
  and and_42 (and_42_out, undriven_22, nor_2_out);
  and and_43 (and_43_out, undriven_15, xor_2_out);
  and and_44 (and_44_out, undriven_15, or_2_out);
  and and_45 (and_45_out, not_23_out, xnor_3_out);
  and and_46 (and_46_out, undriven_23, nor_3_out);
  and and_47 (and_47_out, undriven_23, xor_3_out);
  and and_48 (and_48_out, undriven_16, or_3_out);
  and and_49 (and_49_out, not_24_out, xnor_4_out);
  and and_50 (and_50_out, undriven_24, nor_4_out);
  and and_51 (and_51_out, undriven_17, xor_4_out);
  and and_52 (and_52_out, undriven_17, or_4_out);
  or or_18 (or_18_out, and_132_out, and_131_out);
  and and_53 (and_53_out, and_21_out, not_9_out);
  and and_54 (and_54_out, and_22_out, not_9_out);
  and and_55 (and_55_out, and_23_out, not_17_out);
  and and_56 (and_56_out, and_24_out, or_17_out);
  and and_57 (and_57_out, and_25_out, not_10_out);
  and and_58 (and_58_out, and_26_out, not_10_out);
  and and_59 (and_59_out, and_27_out, not_18_out);
  and and_60 (and_60_out, and_28_out, undriven_18);
  and and_61 (and_61_out, and_29_out, not_11_out);
  and and_62 (and_62_out, and_30_out, not_11_out);
  and and_63 (and_63_out, and_31_out, not_19_out);
  and and_64 (and_64_out, and_32_out, undriven_19);
  and and_65 (and_65_out, and_33_out, not_12_out);
  and and_66 (and_66_out, and_34_out, not_12_out);
  and and_67 (and_67_out, and_35_out, not_20_out);
  and and_68 (and_68_out, and_36_out, undriven_20);
  and and_69 (and_69_out, and_37_out, not_13_out);
  and and_70 (and_70_out, and_38_out, not_13_out);
  and and_71 (and_71_out, and_39_out, not_21_out);
  and and_72 (and_72_out, and_40_out, undriven_21);
  and and_73 (and_73_out, and_41_out, not_14_out);
  and and_74 (and_74_out, and_42_out, not_14_out);
  and and_75 (and_75_out, and_43_out, not_22_out);
  and and_76 (and_76_out, and_44_out, undriven_22);
  and and_77 (and_77_out, and_45_out, not_15_out);
  and and_78 (and_78_out, and_46_out, not_15_out);
  and and_79 (and_79_out, and_47_out, not_23_out);
  and and_80 (and_80_out, and_48_out, undriven_23);
  and and_81 (and_81_out, and_49_out, not_16_out);
  and and_82 (and_82_out, and_50_out, not_16_out);
  and and_83 (and_83_out, and_51_out, not_24_out);
  and and_84 (and_84_out, and_52_out, undriven_24);
  or or_19 (or_19_out, and_132_out, and_131_out);
  or or_20 (or_20_out, and_130_out, and_129_out);
  or or_21 (or_21_out, or_19_out, or_20_out);
  or or_22 (or_22_out, and_53_out, and_54_out);
  or or_23 (or_23_out, and_55_out, and_56_out);
  or or_24 (or_24_out, and_57_out, and_58_out);
  or or_25 (or_25_out, and_59_out, and_60_out);
  or or_26 (or_26_out, and_61_out, and_62_out);
  or or_27 (or_27_out, and_63_out, and_64_out);
  or or_28 (or_28_out, and_65_out, and_66_out);
  or or_29 (or_29_out, and_67_out, and_68_out);
  or or_30 (or_30_out, and_69_out, and_70_out);
  or or_31 (or_31_out, and_71_out, and_72_out);
  or or_32 (or_32_out, and_73_out, and_74_out);
  or or_33 (or_33_out, and_75_out, and_76_out);
  or or_34 (or_34_out, and_77_out, and_78_out);
  or or_35 (or_35_out, and_79_out, and_80_out);
  or or_36 (or_36_out, and_81_out, and_82_out);
  or or_37 (or_37_out, and_83_out, and_84_out);
  or or_38 (or_38_out, or_22_out, or_23_out);
  or or_39 (or_39_out, or_24_out, or_25_out);
  or or_40 (or_40_out, or_26_out, or_27_out);
  or or_41 (or_41_out, or_28_out, or_29_out);
  or or_42 (or_42_out, or_30_out, or_31_out);
  or or_43 (or_43_out, or_32_out, or_33_out);
  or or_44 (or_44_out, or_34_out, or_35_out);
  or or_45 (or_45_out, or_36_out, or_37_out);
  not not_25 (not_25_out, or_21_out);
  and and_85 (and_85_out, or_38_out, not_25_out);
  and and_86 (and_86_out, or_21_out, or_42_out);
  and and_87 (and_87_out, or_39_out, not_25_out);
  and and_88 (and_88_out, or_21_out, or_43_out);
  and and_89 (and_89_out, or_40_out, not_25_out);
  and and_90 (and_90_out, or_21_out, or_44_out);
  and and_91 (and_91_out, or_41_out, not_25_out);
  and and_92 (and_92_out, or_21_out, or_45_out);
  or or_46 (or_46_out, and_85_out, and_86_out);
  or or_47 (or_47_out, and_87_out, and_88_out);
  or or_48 (or_48_out, and_89_out, and_90_out);
  or or_49 (or_49_out, and_91_out, and_92_out);
  not not_26 (not_26_out, undriven_25);
  not not_27 (not_27_out, undriven_26);
  not not_28 (not_28_out, undriven_27);
  not not_29 (not_29_out, undriven_28);
  and and_93 (and_93_out, not_26_out, not_27_out);
  and and_94 (and_94_out, not_26_out, not_27_out);
  and and_95 (and_95_out, not_26_out, not_27_out);
  and and_96 (and_96_out, not_26_out, not_27_out);
  and and_97 (and_97_out, not_26_out, undriven_26);
  and and_98 (and_98_out, not_26_out, undriven_26);
  and and_99 (and_99_out, not_26_out, undriven_26);
  and and_100 (and_100_out, not_26_out, undriven_26);
  and and_101 (and_101_out, undriven_25, not_27_out);
  and and_102 (and_102_out, undriven_25, not_27_out);
  and and_103 (and_103_out, undriven_25, not_27_out);
  and and_104 (and_104_out, undriven_25, not_27_out);
  and and_105 (and_105_out, undriven_25, undriven_26);
  and and_106 (and_106_out, undriven_25, undriven_26);
  and and_107 (and_107_out, undriven_25, undriven_26);
  and and_108 (and_108_out, undriven_25, undriven_26);
  nand nand_5 (nand_5_out, or_46_out, and_133_out);
  nand nand_6 (nand_6_out, or_47_out, and_133_out);
  nand nand_7 (nand_7_out, or_48_out, and_133_out);
  nand nand_8 (nand_8_out, or_49_out, and_133_out);
  and and_109 (and_109_out, and_93_out, not_28_out);
  and and_110 (and_110_out, and_94_out, not_28_out);
  and and_111 (and_111_out, and_95_out, undriven_27);
  and and_112 (and_112_out, and_96_out, undriven_27);
  and and_113 (and_113_out, and_97_out, not_28_out);
  and and_114 (and_114_out, and_98_out, not_28_out);
  and and_115 (and_115_out, and_99_out, undriven_27);
  and and_116 (and_116_out, and_100_out, undriven_27);
  and and_117 (and_117_out, and_101_out, not_28_out);
  and and_118 (and_118_out, and_102_out, not_28_out);
  and and_119 (and_119_out, and_103_out, undriven_27);
  and and_120 (and_120_out, and_104_out, undriven_27);
  and and_121 (and_121_out, and_105_out, not_28_out);
  and and_122 (and_122_out, and_106_out, not_28_out);
  and and_123 (and_123_out, and_107_out, undriven_27);
  and and_124 (and_124_out, and_108_out, undriven_27);
  and and_125 (and_125_out, and_109_out, not_29_out);
  and and_126 (and_126_out, and_110_out, undriven_28);
  and and_127 (and_127_out, and_111_out, not_29_out);
  and and_128 (and_128_out, and_112_out, undriven_28);
  and and_129 (and_129_out, and_113_out, not_29_out);
  and and_130 (and_130_out, and_114_out, undriven_28);
  and and_131 (and_131_out, and_115_out, not_29_out);
  and and_132 (and_132_out, and_116_out, undriven_28);
  and and_133 (and_133_out, and_117_out, not_29_out);
  and and_134 (and_134_out, and_118_out, undriven_28);
  and and_135 (and_135_out, and_119_out, not_29_out);
  and and_136 (and_136_out, and_120_out, undriven_28);
  and and_137 (and_137_out, and_121_out, not_29_out);
  and and_138 (and_138_out, and_122_out, undriven_28);
  and and_139 (and_139_out, and_123_out, not_29_out);
  and and_140 (and_140_out, and_124_out, undriven_28);
  nand nand_9 (nand_9_out, nand_5_out, and_133_out);
  nand nand_10 (nand_10_out, nand_6_out, and_133_out);
  nand nand_11 (nand_11_out, nand_7_out, and_133_out);
  nand nand_12 (nand_12_out, nand_8_out, and_133_out);
  nand nand_13 (nand_13_out, nand_5_out, nand_14_out);
  nand nand_14 (nand_14_out, nand_13_out, nand_9_out);
  nand nand_15 (nand_15_out, nand_6_out, nand_16_out);
  nand nand_16 (nand_16_out, nand_15_out, nand_10_out);
  nand nand_17 (nand_17_out, nand_7_out, nand_18_out);
  nand nand_18 (nand_18_out, nand_17_out, nand_11_out);
  nand nand_19 (nand_19_out, nand_8_out, nand_20_out);
  nand nand_20 (nand_20_out, nand_19_out, nand_12_out);
  not not_30 (not_30_out, undriven_29);
  not not_31 (not_31_out, undriven_30);
  not not_32 (not_32_out, undriven_31);
  and and_141 (and_141_out, not_30_out, not_31_out);
  and and_142 (and_142_out, not_30_out, not_31_out);
  and and_143 (and_143_out, not_30_out, undriven_30);
  and and_144 (and_144_out, not_30_out, undriven_30);
  and and_145 (and_145_out, undriven_29, not_31_out);
  and and_146 (and_146_out, undriven_29, not_31_out);
  and and_147 (and_147_out, undriven_29, undriven_30);
  and and_148 (and_148_out, undriven_29, undriven_30);
  and and_149 (and_149_out, and_141_out, not_32_out);
  and and_150 (and_150_out, and_142_out, undriven_31);
  and and_151 (and_151_out, and_143_out, not_32_out);
  and and_152 (and_152_out, and_144_out, undriven_31);
  and and_153 (and_153_out, and_145_out, not_32_out);
  and and_154 (and_154_out, and_146_out, undriven_31);
  and and_155 (and_155_out, and_147_out, not_32_out);
  and and_156 (and_156_out, and_148_out, undriven_31);
  not not_33 (not_33_out, nand_13_out);
  not not_34 (not_34_out, nand_13_out);
  not not_35 (not_35_out, nand_13_out);
  not not_36 (not_36_out, nand_13_out);
  not not_37 (not_37_out, nand_13_out);
  not not_38 (not_38_out, nand_13_out);
  not not_39 (not_39_out, nand_13_out);
  not not_40 (not_40_out, nand_13_out);
  and and_157 (and_157_out, and_149_out, not_33_out);
  and and_158 (and_158_out, and_149_out, nand_13_out);
  and and_159 (and_159_out, and_150_out, not_34_out);
  and and_160 (and_160_out, and_150_out, nand_13_out);
  and and_161 (and_161_out, and_151_out, not_35_out);
  and and_162 (and_162_out, and_151_out, nand_13_out);
  and and_163 (and_163_out, and_152_out, not_36_out);
  and and_164 (and_164_out, and_152_out, nand_13_out);
  and and_165 (and_165_out, and_153_out, not_37_out);
  and and_166 (and_166_out, and_153_out, nand_13_out);
  and and_167 (and_167_out, and_154_out, not_38_out);
  and and_168 (and_168_out, and_154_out, nand_13_out);
  and and_169 (and_169_out, and_155_out, not_39_out);
  and and_170 (and_170_out, and_155_out, nand_13_out);
  and and_171 (and_171_out, and_156_out, not_40_out);
  and and_172 (and_172_out, and_156_out, nand_13_out);
  and and_173 (and_173_out, and_157_out, not_41_out);
  and and_174 (and_174_out, and_158_out, not_41_out);
  not not_41 (not_41_out, and_134_out);
  and and_175 (and_175_out, and_159_out, not_42_out);
  and and_176 (and_176_out, and_160_out, not_42_out);
  not not_42 (not_42_out, and_134_out);
  and and_177 (and_177_out, and_161_out, not_43_out);
  and and_178 (and_178_out, and_162_out, not_43_out);
  not not_43 (not_43_out, and_134_out);
  and and_179 (and_179_out, and_163_out, not_44_out);
  and and_180 (and_180_out, and_164_out, not_44_out);
  not not_44 (not_44_out, and_134_out);
  and and_181 (and_181_out, and_165_out, not_45_out);
  and and_182 (and_182_out, and_166_out, not_45_out);
  not not_45 (not_45_out, and_134_out);
  and and_183 (and_183_out, and_167_out, not_46_out);
  and and_184 (and_184_out, and_168_out, not_46_out);
  not not_46 (not_46_out, and_134_out);
  and and_185 (and_185_out, and_169_out, not_47_out);
  and and_186 (and_186_out, and_170_out, not_47_out);
  not not_47 (not_47_out, and_134_out);
  and and_187 (and_187_out, and_171_out, not_48_out);
  and and_188 (and_188_out, and_172_out, not_48_out);
  not not_48 (not_48_out, and_134_out);
  nor nor_5 (nor_5_out, and_173_out, nor_6_out);
  nor nor_6 (nor_6_out, nor_5_out, and_174_out);
  nor nor_7 (nor_7_out, and_175_out, nor_8_out);
  nor nor_8 (nor_8_out, nor_7_out, and_176_out);
  nor nor_9 (nor_9_out, and_177_out, nor_10_out);
  nor nor_10 (nor_10_out, nor_9_out, and_178_out);
  nor nor_11 (nor_11_out, and_179_out, nor_12_out);
  nor nor_12 (nor_12_out, nor_11_out, and_180_out);
  nor nor_13 (nor_13_out, and_181_out, nor_14_out);
  nor nor_14 (nor_14_out, nor_13_out, and_182_out);
  nor nor_15 (nor_15_out, and_183_out, nor_16_out);
  nor nor_16 (nor_16_out, nor_15_out, and_184_out);
  nor nor_17 (nor_17_out, and_185_out, nor_18_out);
  nor nor_18 (nor_18_out, nor_17_out, and_186_out);
  nor nor_19 (nor_19_out, and_187_out, nor_20_out);
  nor nor_20 (nor_20_out, nor_19_out, and_188_out);
  and and_189 (and_189_out, and_149_out, nor_5_out);
  and and_190 (and_190_out, and_150_out, nor_7_out);
  and and_191 (and_191_out, and_151_out, nor_9_out);
  and and_192 (and_192_out, and_152_out, nor_11_out);
  and and_193 (and_193_out, and_153_out, nor_13_out);
  and and_194 (and_194_out, and_154_out, nor_15_out);
  and and_195 (and_195_out, and_155_out, nor_17_out);
  and and_196 (and_196_out, and_156_out, nor_19_out);
  and and_197 (and_197_out, and_189_out, and_134_out);
  and and_198 (and_197_out, and_190_out, and_134_out);
  and and_199 (and_197_out, and_191_out, and_134_out);
  and and_200 (and_197_out, and_192_out, and_134_out);
  and and_201 (and_197_out, and_193_out, and_134_out);
  and and_202 (and_197_out, and_194_out, and_134_out);
  and and_203 (and_197_out, and_195_out, and_134_out);
  and and_204 (and_197_out, and_196_out, and_134_out);
  not not_49 (not_49_out, nand_15_out);
  not not_50 (not_50_out, nand_15_out);
  not not_51 (not_51_out, nand_15_out);
  not not_52 (not_52_out, nand_15_out);
  not not_53 (not_53_out, nand_15_out);
  not not_54 (not_54_out, nand_15_out);
  not not_55 (not_55_out, nand_15_out);
  not not_56 (not_56_out, nand_15_out);
  and and_205 (and_205_out, and_149_out, not_49_out);
  and and_206 (and_206_out, and_149_out, nand_15_out);
  not not_57 (not_57_out, and_134_out);
  and and_207 (and_207_out, and_150_out, not_50_out);
  and and_208 (and_208_out, and_150_out, nand_15_out);
  not not_58 (not_58_out, and_134_out);
  and and_209 (and_209_out, and_151_out, not_51_out);
  and and_210 (and_210_out, and_151_out, nand_15_out);
  not not_59 (not_59_out, and_134_out);
  and and_211 (and_211_out, and_152_out, not_52_out);
  and and_212 (and_212_out, and_152_out, nand_15_out);
  not not_60 (not_60_out, and_134_out);
  and and_213 (and_213_out, and_153_out, not_53_out);
  and and_214 (and_214_out, and_153_out, nand_15_out);
  not not_61 (not_61_out, and_134_out);
  and and_215 (and_215_out, and_154_out, not_54_out);
  and and_216 (and_216_out, and_154_out, nand_15_out);
  not not_62 (not_62_out, and_134_out);
  and and_217 (and_217_out, and_155_out, not_55_out);
  and and_218 (and_218_out, and_155_out, nand_15_out);
  not not_63 (not_63_out, and_134_out);
  and and_219 (and_219_out, and_156_out, not_56_out);
  and and_220 (and_220_out, and_156_out, nand_15_out);
  not not_64 (not_64_out, and_134_out);
  and and_221 (and_221_out, and_205_out, not_57_out);
  and and_222 (and_222_out, and_206_out, not_57_out);
  and and_223 (and_223_out, and_207_out, not_58_out);
  and and_224 (and_224_out, and_208_out, not_58_out);
  and and_225 (and_225_out, and_209_out, not_59_out);
  and and_226 (and_226_out, and_210_out, not_59_out);
  and and_227 (and_227_out, and_211_out, not_60_out);
  and and_228 (and_228_out, and_212_out, not_60_out);
  and and_229 (and_229_out, and_213_out, not_61_out);
  and and_230 (and_230_out, and_214_out, not_61_out);
  and and_231 (and_231_out, and_215_out, not_62_out);
  and and_232 (and_232_out, and_216_out, not_62_out);
  and and_233 (and_233_out, and_217_out, not_63_out);
  and and_234 (and_234_out, and_218_out, not_63_out);
  and and_235 (and_235_out, and_219_out, not_64_out);
  and and_236 (and_236_out, and_220_out, not_64_out);
  nor nor_21 (nor_21_out, and_221_out, nor_22_out);
  nor nor_22 (nor_22_out, nor_21_out, and_222_out);
  nor nor_23 (nor_23_out, and_223_out, nor_24_out);
  nor nor_24 (nor_24_out, nor_23_out, and_224_out);
  nor nor_25 (nor_25_out, and_225_out, nor_26_out);
  nor nor_26 (nor_26_out, nor_25_out, and_226_out);
  nor nor_27 (nor_27_out, and_227_out, nor_28_out);
  nor nor_28 (nor_28_out, nor_27_out, and_228_out);
  nor nor_29 (nor_29_out, and_229_out, nor_30_out);
  nor nor_30 (nor_30_out, nor_29_out, and_230_out);
  nor nor_31 (nor_31_out, and_231_out, nor_32_out);
  nor nor_32 (nor_32_out, nor_31_out, and_232_out);
  nor nor_33 (nor_33_out, and_233_out, nor_34_out);
  nor nor_34 (nor_34_out, nor_33_out, and_234_out);
  nor nor_35 (nor_35_out, and_235_out, nor_36_out);
  nor nor_36 (nor_36_out, nor_35_out, and_236_out);
  and and_237 (and_237_out, and_149_out, nor_21_out);
  and and_238 (and_238_out, and_150_out, nor_23_out);
  and and_239 (and_239_out, and_151_out, nor_25_out);
  and and_240 (and_240_out, and_152_out, nor_27_out);
  and and_241 (and_241_out, and_153_out, nor_29_out);
  and and_242 (and_242_out, and_154_out, nor_31_out);
  and and_243 (and_243_out, and_155_out, nor_33_out);
  and and_244 (and_244_out, and_156_out, nor_35_out);
  and and_245 (and_245_out, and_237_out, and_134_out);
  and and_246 (and_245_out, and_238_out, and_134_out);
  and and_247 (and_245_out, and_239_out, and_134_out);
  and and_248 (and_245_out, and_240_out, and_134_out);
  and and_249 (and_245_out, and_241_out, and_134_out);
  and and_250 (and_245_out, and_242_out, and_134_out);
  and and_251 (and_245_out, and_243_out, and_134_out);
  and and_252 (and_245_out, and_244_out, and_134_out);
  not not_65 (not_65_out, nand_17_out);
  not not_66 (not_66_out, nand_17_out);
  not not_67 (not_67_out, nand_17_out);
  not not_68 (not_68_out, nand_17_out);
  not not_69 (not_69_out, nand_17_out);
  not not_70 (not_70_out, nand_17_out);
  not not_71 (not_71_out, nand_17_out);
  not not_72 (not_72_out, nand_17_out);
  and and_253 (and_253_out, and_149_out, not_65_out);
  and and_254 (and_254_out, and_149_out, nand_17_out);
  and and_255 (and_255_out, and_150_out, not_66_out);
  and and_256 (and_256_out, and_150_out, nand_17_out);
  and and_257 (and_257_out, and_151_out, not_67_out);
  and and_258 (and_258_out, and_151_out, nand_17_out);
  and and_259 (and_259_out, and_152_out, not_68_out);
  and and_260 (and_260_out, and_152_out, nand_17_out);
  and and_261 (and_261_out, and_153_out, not_69_out);
  and and_262 (and_262_out, and_153_out, nand_17_out);
  and and_263 (and_263_out, and_154_out, not_70_out);
  and and_264 (and_264_out, and_154_out, nand_17_out);
  and and_265 (and_265_out, and_155_out, not_71_out);
  and and_266 (and_266_out, and_155_out, nand_17_out);
  and and_267 (and_267_out, and_156_out, not_72_out);
  and and_268 (and_268_out, and_156_out, nand_17_out);
  and and_269 (and_269_out, and_253_out, not_73_out);
  and and_270 (and_270_out, and_254_out, not_73_out);
  not not_73 (not_73_out, and_134_out);
  and and_271 (and_271_out, and_255_out, not_74_out);
  and and_272 (and_272_out, and_256_out, not_74_out);
  not not_74 (not_74_out, and_134_out);
  and and_273 (and_273_out, and_257_out, not_75_out);
  and and_274 (and_274_out, and_258_out, not_75_out);
  not not_75 (not_75_out, and_134_out);
  and and_275 (and_275_out, and_259_out, not_76_out);
  and and_276 (and_276_out, and_260_out, not_76_out);
  not not_76 (not_76_out, and_134_out);
  and and_277 (and_277_out, and_261_out, not_77_out);
  and and_278 (and_278_out, and_262_out, not_77_out);
  not not_77 (not_77_out, and_134_out);
  and and_279 (and_279_out, and_263_out, not_78_out);
  and and_280 (and_280_out, and_264_out, not_78_out);
  not not_78 (not_78_out, and_134_out);
  and and_281 (and_281_out, and_265_out, not_79_out);
  and and_282 (and_282_out, and_266_out, not_79_out);
  not not_79 (not_79_out, and_134_out);
  and and_283 (and_283_out, and_267_out, not_80_out);
  and and_284 (and_284_out, and_268_out, not_80_out);
  not not_80 (not_80_out, and_134_out);
  nor nor_37 (nor_37_out, and_269_out, nor_38_out);
  nor nor_38 (nor_38_out, nor_37_out, and_270_out);
  nor nor_39 (nor_39_out, and_271_out, nor_40_out);
  nor nor_40 (nor_40_out, nor_39_out, and_272_out);
  nor nor_41 (nor_41_out, and_273_out, nor_42_out);
  nor nor_42 (nor_42_out, nor_41_out, and_274_out);
  nor nor_43 (nor_43_out, and_275_out, nor_44_out);
  nor nor_44 (nor_44_out, nor_43_out, and_276_out);
  nor nor_45 (nor_45_out, and_277_out, nor_46_out);
  nor nor_46 (nor_46_out, nor_45_out, and_278_out);
  nor nor_47 (nor_47_out, and_279_out, nor_48_out);
  nor nor_48 (nor_48_out, nor_47_out, and_280_out);
  nor nor_49 (nor_49_out, and_281_out, nor_50_out);
  nor nor_50 (nor_50_out, nor_49_out, and_282_out);
  nor nor_51 (nor_51_out, and_283_out, nor_52_out);
  nor nor_52 (nor_52_out, nor_51_out, and_284_out);
  and and_285 (and_285_out, and_149_out, nor_37_out);
  and and_286 (and_286_out, and_150_out, nor_39_out);
  and and_287 (and_287_out, and_151_out, nor_41_out);
  and and_288 (and_288_out, and_152_out, nor_43_out);
  and and_289 (and_289_out, and_153_out, nor_45_out);
  and and_290 (and_290_out, and_154_out, nor_47_out);
  and and_291 (and_291_out, and_155_out, nor_49_out);
  and and_292 (and_292_out, and_156_out, nor_51_out);
  and and_293 (and_293_out, and_285_out, and_134_out);
  and and_294 (and_293_out, and_286_out, and_134_out);
  and and_295 (and_293_out, and_287_out, and_134_out);
  and and_296 (and_293_out, and_288_out, and_134_out);
  and and_297 (and_293_out, and_289_out, and_134_out);
  and and_298 (and_293_out, and_290_out, and_134_out);
  and and_299 (and_293_out, and_291_out, and_134_out);
  and and_300 (and_293_out, and_292_out, and_134_out);
  not not_81 (not_81_out, nand_19_out);
  not not_82 (not_82_out, nand_19_out);
  not not_83 (not_83_out, nand_19_out);
  not not_84 (not_84_out, nand_19_out);
  not not_85 (not_85_out, nand_19_out);
  not not_86 (not_86_out, nand_19_out);
  not not_87 (not_87_out, nand_19_out);
  not not_88 (not_88_out, nand_19_out);
  and and_301 (and_301_out, and_149_out, not_81_out);
  and and_302 (and_302_out, and_149_out, nand_19_out);
  not not_89 (not_89_out, and_134_out);
  and and_303 (and_303_out, and_150_out, not_82_out);
  and and_304 (and_304_out, and_150_out, nand_19_out);
  not not_90 (not_90_out, and_134_out);
  and and_305 (and_305_out, and_151_out, not_83_out);
  and and_306 (and_306_out, and_151_out, nand_19_out);
  not not_91 (not_91_out, and_134_out);
  and and_307 (and_307_out, and_152_out, not_84_out);
  and and_308 (and_308_out, and_152_out, nand_19_out);
  not not_92 (not_92_out, and_134_out);
  and and_309 (and_309_out, and_153_out, not_85_out);
  and and_310 (and_310_out, and_153_out, nand_19_out);
  not not_93 (not_93_out, and_134_out);
  and and_311 (and_311_out, and_154_out, not_86_out);
  and and_312 (and_312_out, and_154_out, nand_19_out);
  not not_94 (not_94_out, and_134_out);
  and and_313 (and_313_out, and_155_out, not_87_out);
  and and_314 (and_314_out, and_155_out, nand_19_out);
  not not_95 (not_95_out, and_134_out);
  and and_315 (and_315_out, and_156_out, not_88_out);
  and and_316 (and_316_out, and_156_out, nand_19_out);
  not not_96 (not_96_out, and_134_out);
  and and_317 (and_317_out, and_301_out, not_89_out);
  and and_318 (and_318_out, and_302_out, not_89_out);
  and and_319 (and_319_out, and_303_out, not_90_out);
  and and_320 (and_320_out, and_304_out, not_90_out);
  and and_321 (and_321_out, and_305_out, not_91_out);
  and and_322 (and_322_out, and_306_out, not_91_out);
  and and_323 (and_323_out, and_307_out, not_92_out);
  and and_324 (and_324_out, and_308_out, not_92_out);
  and and_325 (and_325_out, and_309_out, not_93_out);
  and and_326 (and_326_out, and_310_out, not_93_out);
  and and_327 (and_327_out, and_311_out, not_94_out);
  and and_328 (and_328_out, and_312_out, not_94_out);
  and and_329 (and_329_out, and_313_out, not_95_out);
  and and_330 (and_330_out, and_314_out, not_95_out);
  and and_331 (and_331_out, and_315_out, not_96_out);
  and and_332 (and_332_out, and_316_out, not_96_out);
  nor nor_53 (nor_53_out, and_317_out, nor_54_out);
  nor nor_54 (nor_54_out, nor_53_out, and_318_out);
  nor nor_55 (nor_55_out, and_319_out, nor_56_out);
  nor nor_56 (nor_56_out, nor_55_out, and_320_out);
  nor nor_57 (nor_57_out, and_321_out, nor_58_out);
  nor nor_58 (nor_58_out, nor_57_out, and_322_out);
  nor nor_59 (nor_59_out, and_323_out, nor_60_out);
  nor nor_60 (nor_60_out, nor_59_out, and_324_out);
  nor nor_61 (nor_61_out, and_325_out, nor_62_out);
  nor nor_62 (nor_62_out, nor_61_out, and_326_out);
  nor nor_63 (nor_63_out, and_327_out, nor_64_out);
  nor nor_64 (nor_64_out, nor_63_out, and_328_out);
  nor nor_65 (nor_65_out, and_329_out, nor_66_out);
  nor nor_66 (nor_66_out, nor_65_out, and_330_out);
  nor nor_67 (nor_67_out, and_331_out, nor_68_out);
  nor nor_68 (nor_68_out, nor_67_out, and_332_out);
  and and_333 (and_333_out, and_149_out, nor_53_out);
  and and_334 (and_334_out, and_150_out, nor_55_out);
  and and_335 (and_335_out, and_151_out, nor_57_out);
  and and_336 (and_336_out, and_152_out, nor_59_out);
  and and_337 (and_337_out, and_153_out, nor_61_out);
  and and_338 (and_338_out, and_154_out, nor_63_out);
  and and_339 (and_339_out, and_155_out, nor_65_out);
  and and_340 (and_340_out, and_156_out, nor_67_out);
  and and_341 (and_341_out, and_333_out, and_134_out);
  and and_342 (and_341_out, and_334_out, and_134_out);
  and and_343 (and_341_out, and_335_out, and_134_out);
  and and_344 (and_341_out, and_336_out, and_134_out);
  and and_345 (and_341_out, and_337_out, and_134_out);
  and and_346 (and_341_out, and_338_out, and_134_out);
  and and_347 (and_341_out, and_339_out, and_134_out);
  and and_348 (and_341_out, and_340_out, and_134_out);

  // Notes on the sheet:
  //   0000 - ADD
  //   0001 - SUB
  //   0010 - A AND B
  //   0011 - A NAND B
  //   0100 - A XNOR B
  //   0101 - A NOR B
  //   0110 - A XOR B
  //   0111 - A OR B
  //   1000 -
  //   1001 - READ/WRITE
  //   CLOCK CACHE
endmodule
