// Digital circuit 8 bit CPU.dig as structural Verilog
module _8_bit_CPU (
);

  wire and_1_out, and_2_out, and_3_out, and_4_out, and_5_out, and_6_out, and_7_out, and_8_out, and_9_out,
       and_10_out, and_11_out, and_12_out, and_13_out, and_14_out, and_15_out, and_16_out, and_17_out,
       and_18_out, and_19_out, and_20_out, and_21_out, and_22_out, and_23_out, and_24_out, and_25_out,
       and_26_out, and_27_out, and_28_out, and_29_out, and_30_out, and_31_out, and_32_out, and_33_out,
       and_34_out, and_35_out, and_36_out, and_37_out, and_38_out, and_39_out, and_40_out, and_41_out,
       and_42_out, and_43_out, and_44_out, and_45_out, and_46_out, and_47_out, and_48_out, and_49_out,
       and_50_out, and_51_out, and_52_out, and_53_out, and_54_out, and_55_out, and_56_out, and_57_out,
       and_58_out, and_59_out, and_60_out, and_61_out, and_62_out, and_63_out, and_64_out, and_65_out,
       and_66_out, and_67_out, and_68_out, and_69_out, and_70_out, and_71_out, and_72_out, and_73_out,
       and_74_out, and_75_out, and_76_out, and_77_out, and_78_out, and_79_out, and_80_out, and_81_out,
       and_82_out, and_83_out, and_84_out, and_85_out, and_86_out, and_87_out, and_88_out, and_89_out,
       and_90_out, and_91_out, and_92_out, and_93_out, and_94_out, and_95_out, and_96_out, and_97_out,
       and_98_out, and_99_out, and_100_out, and_101_out, and_102_out, and_103_out, and_104_out, and_106_out,
       and_107_out, and_108_out, and_109_out, and_111_out, and_113_out, and_114_out, and_115_out,
       and_116_out, and_117_out, and_118_out, and_119_out, and_120_out, and_121_out, and_122_out,
       and_123_out, and_124_out, and_125_out, and_126_out, and_127_out, and_128_out, and_129_out,
       and_130_out, and_131_out, and_132_out, and_133_out, and_134_out, and_135_out, and_136_out,
       and_137_out, and_138_out, and_139_out, and_140_out, and_141_out, and_142_out, and_143_out,
       and_144_out, and_145_out, and_146_out, and_147_out, and_148_out, and_149_out, and_150_out,
       and_151_out, and_152_out, and_153_out, and_154_out, and_155_out, and_156_out, and_157_out,
       and_158_out, and_159_out, and_160_out, and_162_out, and_163_out, and_164_out, and_165_out,
       and_166_out, and_167_out, and_168_out, and_169_out, and_170_out, and_171_out, and_172_out,
       and_173_out, and_174_out, and_175_out, and_176_out, and_177_out, and_178_out, and_179_out,
       and_180_out, and_181_out, and_182_out, and_183_out, and_184_out, and_185_out, and_186_out,
       and_187_out, and_188_out, and_189_out, and_190_out, and_191_out, and_192_out, and_193_out,
       and_194_out, and_195_out, and_196_out, and_197_out, and_198_out, and_199_out, and_200_out,
       and_201_out, and_202_out, and_203_out, and_204_out, and_205_out, and_206_out, and_207_out,
       and_208_out, and_209_out, and_210_out, and_211_out, and_212_out, and_213_out, and_214_out,
       and_215_out, and_216_out, and_217_out, and_218_out, and_219_out, and_220_out, and_221_out,
       and_222_out, and_223_out, and_224_out, and_225_out, and_226_out, and_227_out, and_228_out,
       and_229_out, and_230_out, and_231_out, and_232_out, and_233_out, and_234_out, and_235_out,
       and_236_out, and_237_out, and_238_out, and_239_out, and_240_out, and_241_out, and_242_out,
       and_243_out, and_244_out, and_245_out, and_246_out, and_247_out, and_248_out, and_249_out,
       and_250_out, and_251_out, and_252_out, and_253_out, and_254_out, and_255_out, and_256_out,
       and_257_out, and_258_out, and_259_out, and_260_out, and_261_out, and_262_out, and_263_out,
       and_264_out, and_265_out, and_266_out, and_267_out, and_268_out, and_269_out, and_270_out,
       and_271_out, and_272_out, and_273_out, and_274_out, and_275_out, and_276_out, and_277_out,
       and_278_out, and_279_out, and_280_out, and_281_out, and_282_out, and_283_out, and_284_out,
       and_285_out, and_286_out, and_287_out, and_288_out, and_289_out, and_290_out, and_291_out,
       and_292_out, and_293_out, and_294_out, and_295_out, and_296_out, and_297_out, and_298_out,
       and_299_out, and_300_out, and_301_out, and_302_out, and_303_out, and_304_out, and_305_out,
       and_306_out, and_307_out, and_308_out, and_309_out, and_310_out, and_311_out, and_312_out,
       and_313_out, and_314_out, and_315_out, and_316_out, and_317_out, and_318_out, and_319_out,
       and_320_out, and_321_out, and_322_out, and_323_out, and_324_out, and_325_out, and_326_out,
       and_327_out, and_328_out, and_329_out, and_330_out, and_331_out, and_332_out, and_333_out,
       and_334_out, and_335_out, and_336_out, and_337_out, and_338_out, and_339_out, and_340_out,
       and_341_out, and_342_out, and_343_out, and_344_out, and_345_out, and_346_out, and_347_out,
       and_348_out, and_349_out, and_350_out, and_351_out, and_352_out, and_353_out, and_354_out,
       and_355_out, and_356_out, and_357_out, and_358_out, and_359_out, and_360_out, and_361_out,
       and_362_out, and_363_out, and_364_out, and_365_out, and_366_out, and_367_out, and_368_out,
       and_369_out, and_370_out, and_371_out, and_372_out, and_373_out, and_374_out, and_375_out,
       and_376_out, and_377_out, and_378_out, and_379_out, and_380_out, and_381_out, and_382_out,
       and_383_out, and_384_out, and_385_out, and_386_out, and_387_out, and_388_out, and_389_out,
       and_390_out, and_391_out, and_392_out, and_393_out, and_394_out, and_395_out, and_396_out,
       and_397_out, and_398_out, and_399_out, and_400_out, and_401_out, and_402_out, and_403_out,
       and_404_out, and_405_out, and_406_out, and_407_out, and_408_out, and_409_out, and_410_out,
       and_411_out, and_412_out, and_413_out, and_414_out, and_415_out, and_416_out, and_417_out,
       and_418_out, and_419_out, and_420_out, and_421_out, and_422_out, and_423_out, and_424_out,
       and_425_out, and_426_out, and_427_out, and_428_out, and_429_out, and_430_out, and_431_out,
       and_432_out, and_433_out, and_434_out, and_435_out, and_436_out, and_437_out, and_438_out,
       and_439_out, and_440_out, and_441_out, and_442_out, and_443_out, and_444_out, and_445_out,
       and_446_out, and_447_out, and_448_out, and_449_out, and_450_out, and_451_out, and_452_out,
       and_453_out, and_454_out, and_455_out, and_456_out, and_457_out, and_458_out, and_459_out,
       and_460_out, and_461_out, and_462_out, and_463_out, and_464_out, and_465_out, and_466_out,
       and_467_out, and_468_out, and_469_out, and_470_out, and_471_out, and_472_out, and_473_out,
       and_474_out, and_475_out, and_476_out, and_477_out, and_478_out, and_479_out, and_480_out,
       and_481_out, and_482_out, and_483_out, and_484_out, and_485_out, and_486_out, and_487_out,
       and_488_out, and_489_out, and_490_out, and_491_out, and_492_out, and_493_out, and_494_out,
       and_495_out, and_496_out, and_497_out, and_498_out, and_499_out, and_500_out, and_501_out,
       and_502_out, and_503_out, and_504_out, button_1_out, dipswitch_1_out, dipswitch_2_out,
       dipswitch_3_out, dipswitch_4_out, dipswitch_5_out, dipswitch_6_out, dipswitch_7_out, dipswitch_8_out,
       dipswitch_9_out, dipswitch_10_out, dipswitch_11_out, dipswitch_12_out, dipswitch_13_out,
       dipswitch_14_out, dipswitch_16_out, dipswitch_17_out, dipswitch_18_out, dipswitch_19_out,
       dipswitch_20_out, dipswitch_21_out, dipswitch_22_out, dipswitch_23_out, dipswitch_24_out,
       dipswitch_25_out, dipswitch_26_out, dipswitch_27_out, dipswitch_28_out, dipswitch_29_out,
       dipswitch_30_out, dipswitch_31_out, dipswitch_32_out, nand_1_out, nand_2_out, nand_3_out, nand_4_out,
       nand_5_out, nand_6_out, nand_7_out, nand_8_out, nand_9_out, nand_10_out, nand_11_out, nand_12_out,
       nand_13_out, nand_14_out, nand_15_out, nand_16_out, nand_17_out, nand_18_out, nand_19_out,
       nand_20_out, nand_21_out, nand_22_out, nand_23_out, nand_24_out, nand_25_out, nand_26_out,
       nand_27_out, nand_28_out, nand_29_out, nand_30_out, nand_31_out, nand_32_out, nor_1_out, nor_2_out,
       nor_3_out, nor_4_out, nor_5_out, nor_6_out, nor_7_out, nor_8_out, nor_9_out, nor_10_out, nor_11_out,
       nor_12_out, nor_13_out, nor_14_out, nor_15_out, nor_16_out, nor_17_out, nor_18_out, nor_19_out,
       nor_20_out, nor_21_out, nor_22_out, nor_23_out, nor_24_out, nor_25_out, nor_26_out, nor_27_out,
       nor_28_out, nor_29_out, nor_30_out, nor_31_out, nor_32_out, nor_33_out, nor_34_out, nor_35_out,
       nor_36_out, nor_37_out, nor_38_out, nor_39_out, nor_40_out, nor_41_out, nor_42_out, nor_43_out,
       nor_44_out, nor_45_out, nor_46_out, nor_47_out, nor_48_out, nor_49_out, nor_50_out, nor_51_out,
       nor_52_out, nor_53_out, nor_54_out, nor_55_out, nor_56_out, nor_57_out, nor_58_out, nor_59_out,
       nor_60_out, nor_61_out, nor_62_out, nor_63_out, nor_64_out, nor_65_out, nor_66_out, nor_67_out,
       nor_68_out, nor_69_out, nor_70_out, nor_71_out, nor_72_out, nor_73_out, nor_74_out, nor_75_out,
       nor_76_out, nor_77_out, nor_78_out, nor_79_out, nor_80_out, nor_81_out, nor_82_out, nor_83_out,
       nor_84_out, nor_85_out, nor_86_out, nor_87_out, nor_88_out, nor_89_out, nor_90_out, nor_91_out,
       nor_92_out, nor_93_out, nor_94_out, nor_95_out, nor_96_out, nor_97_out, nor_98_out, nor_99_out,
       nor_100_out, nor_101_out, nor_102_out, nor_103_out, nor_104_out, nor_105_out, nor_106_out,
       nor_107_out, nor_108_out, nor_109_out, nor_110_out, nor_111_out, nor_112_out, not_1_out, not_2_out,
       not_3_out, not_4_out, not_5_out, not_6_out, not_7_out, not_8_out, not_9_out, not_10_out, not_11_out,
       not_12_out, not_13_out, not_14_out, not_15_out, not_16_out, not_17_out, not_18_out, not_19_out,
       not_20_out, not_21_out, not_22_out, not_23_out, not_24_out, not_25_out, not_26_out, not_27_out,
       not_28_out, not_29_out, not_30_out, not_31_out, not_32_out, not_33_out, not_34_out, not_35_out,
       not_36_out, not_37_out, not_38_out, not_39_out, not_40_out, not_41_out, not_42_out, not_43_out,
       not_44_out, not_45_out, not_46_out, not_47_out, not_48_out, not_49_out, not_50_out, not_51_out,
       not_52_out, not_53_out, not_54_out, not_55_out, not_56_out, not_57_out, not_58_out, not_59_out,
       not_60_out, not_61_out, not_62_out, not_63_out, not_64_out, not_65_out, not_66_out, not_67_out,
       not_68_out, not_69_out, not_70_out, not_71_out, not_72_out, not_73_out, not_74_out, not_75_out,
       not_76_out, not_77_out, not_78_out, not_79_out, not_80_out, not_81_out, not_82_out, not_83_out,
       not_84_out, not_85_out, not_86_out, not_87_out, not_88_out, not_89_out, not_90_out, not_91_out,
       not_92_out, not_93_out, not_94_out, not_95_out, not_96_out, not_97_out, not_98_out, not_99_out,
       not_100_out, not_101_out, not_102_out, not_103_out, not_104_out, not_105_out, not_106_out,
       not_107_out, not_108_out, not_109_out, not_110_out, not_111_out, not_112_out, not_113_out,
       not_114_out, not_115_out, not_116_out, not_117_out, not_118_out, not_119_out, not_120_out,
       not_121_out, not_122_out, not_123_out, not_124_out, not_125_out, not_126_out, not_127_out,
       not_128_out, not_129_out, not_130_out, not_131_out, not_132_out, not_133_out, not_134_out,
       not_135_out, not_136_out, not_137_out, not_138_out, not_139_out, not_140_out, not_141_out,
       not_142_out, not_143_out, not_144_out, not_145_out, not_146_out, not_147_out, not_148_out,
       not_149_out, not_150_out, not_151_out, not_152_out, not_153_out, not_154_out, not_155_out,
       not_156_out, not_157_out, not_158_out, not_159_out, not_160_out, not_161_out, not_162_out,
       not_163_out, not_164_out, not_165_out, not_166_out, not_167_out, or_1_out, or_2_out, or_3_out,
       or_4_out, or_5_out, or_6_out, or_7_out, or_8_out, or_9_out, or_10_out, or_11_out, or_12_out,
       or_13_out, or_14_out, or_15_out, or_16_out, or_17_out, or_18_out, or_19_out, or_20_out, or_21_out,
       or_22_out, or_23_out, or_24_out, or_25_out, or_26_out, or_27_out, or_28_out, or_29_out, or_30_out,
       or_31_out, or_32_out, or_33_out, or_34_out, or_35_out, or_36_out, or_37_out, or_38_out, or_39_out,
       or_40_out, or_41_out, or_42_out, or_43_out, or_44_out, or_45_out, or_46_out, or_47_out, or_48_out,
       or_49_out, or_50_out, or_51_out, or_52_out, or_53_out, or_54_out, or_55_out, or_56_out, or_57_out,
       or_58_out, or_59_out, or_60_out, or_61_out, or_62_out, or_63_out, or_64_out, or_65_out, or_66_out,
       or_67_out, or_68_out, or_69_out, or_70_out, or_71_out, or_72_out, or_73_out, or_74_out, or_75_out,
       or_76_out, or_77_out, or_79_out, or_81_out, or_82_out, or_83_out, or_84_out, or_85_out, or_86_out,
       or_87_out, or_88_out, or_89_out, or_90_out, or_91_out, or_92_out, or_93_out, or_94_out, or_95_out,
       or_96_out, or_97_out, or_98_out, or_99_out, or_100_out, or_101_out, or_102_out, or_103_out,
       or_104_out, or_105_out, or_106_out, or_107_out, or_108_out, or_109_out, or_110_out, or_111_out,
       or_112_out, or_113_out, or_114_out, or_115_out, or_116_out, or_117_out, or_118_out, or_119_out,
       or_120_out, or_121_out, or_122_out, or_123_out, or_124_out, or_125_out, or_126_out, or_127_out,
       or_128_out, xor_1_out, xor_2_out, xor_3_out, xor_4_out, xor_5_out, xor_6_out, xor_7_out, xor_8_out,
       xor_9_out, xor_10_out, xor_11_out, xor_12_out, xor_13_out, xor_14_out, xor_15_out, xor_16_out,
       xor_17_out, xor_18_out, xor_19_out, xor_20_out, xor_21_out, xor_22_out, xor_23_out, xor_24_out,
       xor_25_out, xor_26_out, xor_27_out, xor_28_out, xor_29_out, xor_30_out, xor_31_out, xor_32_out,
       xor_33_out, xor_34_out, xor_35_out, xor_36_out, xor_37_out, xor_38_out, xor_39_out, xor_40_out;

  and and_1 (and_1_out, dipswitch_32_out, dipswitch_24_out);
  and and_2 (and_2_out, dipswitch_31_out, dipswitch_23_out);
  and and_3 (and_3_out, dipswitch_30_out, dipswitch_22_out);
  and and_4 (and_4_out, dipswitch_29_out, dipswitch_21_out);
  and and_5 (and_5_out, dipswitch_28_out, dipswitch_20_out);
  and and_6 (and_6_out, dipswitch_27_out, dipswitch_19_out);
  and and_7 (and_7_out, dipswitch_26_out, dipswitch_18_out);
  and and_8 (and_8_out, dipswitch_25_out, dipswitch_17_out);
  or or_1 (or_1_out, dipswitch_32_out, dipswitch_24_out);
  or or_2 (or_2_out, dipswitch_31_out, dipswitch_23_out);
  or or_3 (or_3_out, dipswitch_30_out, dipswitch_22_out);
  or or_4 (or_4_out, dipswitch_29_out, dipswitch_21_out);
  or or_5 (or_5_out, dipswitch_28_out, dipswitch_20_out);
  or or_6 (or_6_out, dipswitch_27_out, dipswitch_19_out);
  or or_7 (or_7_out, dipswitch_26_out, dipswitch_18_out);
  or or_8 (or_8_out, dipswitch_25_out, dipswitch_17_out);
  xor xor_1 (xor_1_out, dipswitch_32_out, dipswitch_24_out);
  xor xor_2 (xor_2_out, dipswitch_31_out, dipswitch_23_out);
  xor xor_3 (xor_3_out, dipswitch_30_out, dipswitch_22_out);
  xor xor_4 (xor_4_out, dipswitch_29_out, dipswitch_21_out);
  xor xor_5 (xor_5_out, dipswitch_28_out, dipswitch_20_out);
  xor xor_6 (xor_6_out, dipswitch_27_out, dipswitch_19_out);
  xor xor_7 (xor_7_out, dipswitch_26_out, dipswitch_18_out);
  xor xor_8 (xor_8_out, dipswitch_25_out, dipswitch_17_out);
  DipSwitch dipswitch_1 (.out(dipswitch_1_out));
  DipSwitch dipswitch_2 (.out(dipswitch_2_out));
  DipSwitch dipswitch_3 (.out(dipswitch_3_out));
  DipSwitch dipswitch_4 (.out(dipswitch_4_out));
  DipSwitch dipswitch_5 (.out(dipswitch_5_out));
  DipSwitch dipswitch_6 (.out(dipswitch_6_out));
  DipSwitch dipswitch_7 (.out(dipswitch_7_out));
  DipSwitch dipswitch_8 (.out(dipswitch_8_out));
  DipSwitch dipswitch_9 (.out(dipswitch_9_out));
  Button button_1 (.out(button_1_out));
  not not_1 (not_1_out, dipswitch_24_out);
  not not_2 (not_2_out, dipswitch_23_out);
  not not_3 (not_3_out, dipswitch_22_out);
  not not_4 (not_4_out, dipswitch_21_out);
  not not_5 (not_5_out, dipswitch_20_out);
  not not_6 (not_6_out, dipswitch_19_out);
  not not_7 (not_7_out, dipswitch_18_out);
  not not_8 (not_8_out, dipswitch_17_out);
  xor xor_9 (xor_9_out, dipswitch_24_out, dipswitch_25_out);
  xor xor_10 (xor_10_out, dipswitch_23_out, dipswitch_31_out);
  xor xor_11 (xor_11_out, dipswitch_22_out, dipswitch_30_out);
  xor xor_12 (xor_12_out, dipswitch_21_out, dipswitch_29_out);
  xor xor_13 (xor_13_out, dipswitch_20_out, dipswitch_28_out);
  xor xor_14 (xor_14_out, dipswitch_19_out, dipswitch_27_out);
  xor xor_15 (xor_15_out, dipswitch_18_out, dipswitch_26_out);
  xor xor_16 (xor_16_out, dipswitch_17_out, dipswitch_25_out);
  xor xor_17 (xor_17_out, dipswitch_24_out, dipswitch_32_out);
  xor xor_18 (xor_18_out, dipswitch_23_out, dipswitch_31_out);
  xor xor_19 (xor_19_out, dipswitch_22_out, dipswitch_30_out);
  xor xor_20 (xor_20_out, dipswitch_21_out, dipswitch_29_out);
  xor xor_21 (xor_21_out, dipswitch_20_out, dipswitch_28_out);
  xor xor_22 (xor_22_out, dipswitch_19_out, dipswitch_27_out);
  xor xor_23 (xor_23_out, dipswitch_18_out, dipswitch_26_out);
  xor xor_24 (xor_24_out, dipswitch_17_out, dipswitch_25_out);
  not not_9 (not_9_out, xor_17_out);
  not not_10 (not_10_out, xor_18_out);
  not not_11 (not_11_out, xor_19_out);
  not not_12 (not_12_out, xor_20_out);
  not not_13 (not_13_out, xor_21_out);
  not not_14 (not_14_out, xor_22_out);
  not not_15 (not_15_out, xor_23_out);
  not not_16 (not_16_out, xor_24_out);
  xor xor_25 (xor_25_out, xor_9_out, dipswitch_32_out);
  and and_9 (and_9_out, dipswitch_32_out, xor_9_out);
  and and_10 (and_10_out, dipswitch_25_out, dipswitch_24_out);
  xor xor_26 (xor_26_out, xor_10_out, or_9_out);
  and and_11 (and_11_out, or_9_out, xor_10_out);
  and and_12 (and_12_out, dipswitch_31_out, dipswitch_23_out);
  xor xor_27 (xor_27_out, xor_11_out, or_10_out);
  and and_13 (and_13_out, or_10_out, xor_11_out);
  and and_14 (and_14_out, dipswitch_30_out, dipswitch_22_out);
  xor xor_28 (xor_28_out, xor_12_out, or_11_out);
  and and_15 (and_15_out, or_11_out, xor_12_out);
  and and_16 (and_16_out, dipswitch_29_out, dipswitch_21_out);
  xor xor_29 (xor_29_out, xor_13_out, or_12_out);
  and and_17 (and_17_out, or_12_out, xor_13_out);
  and and_18 (and_18_out, dipswitch_28_out, dipswitch_20_out);
  xor xor_30 (xor_30_out, xor_14_out, or_13_out);
  and and_19 (and_19_out, or_13_out, xor_14_out);
  and and_20 (and_20_out, dipswitch_27_out, dipswitch_19_out);
  xor xor_31 (xor_31_out, xor_15_out, or_14_out);
  and and_21 (and_21_out, or_14_out, xor_15_out);
  and and_22 (and_22_out, dipswitch_26_out, dipswitch_18_out);
  xor xor_32 (xor_32_out, xor_16_out, or_15_out);
  and and_23 (and_23_out, or_15_out, xor_16_out);
  and and_24 (and_24_out, dipswitch_25_out, dipswitch_17_out);
  xor xor_33 (xor_33_out, xor_17_out, button_1_out);
  and and_25 (and_25_out, button_1_out, not_9_out);
  and and_26 (and_26_out, dipswitch_32_out, not_1_out);
  xor xor_34 (xor_34_out, xor_18_out, or_17_out);
  and and_27 (and_27_out, or_17_out, not_10_out);
  and and_28 (and_28_out, dipswitch_31_out, not_2_out);
  xor xor_35 (xor_35_out, xor_19_out, or_18_out);
  and and_29 (and_29_out, or_18_out, not_11_out);
  and and_30 (and_30_out, dipswitch_30_out, not_3_out);
  xor xor_36 (xor_36_out, xor_20_out, or_19_out);
  and and_31 (and_31_out, or_19_out, not_12_out);
  and and_32 (and_32_out, dipswitch_29_out, not_4_out);
  xor xor_37 (xor_37_out, xor_21_out, or_20_out);
  and and_33 (and_33_out, or_20_out, not_13_out);
  and and_34 (and_34_out, dipswitch_28_out, not_5_out);
  xor xor_38 (xor_38_out, xor_22_out, or_21_out);
  and and_35 (and_35_out, or_21_out, not_14_out);
  and and_36 (and_36_out, dipswitch_27_out, not_6_out);
  xor xor_39 (xor_39_out, xor_23_out, or_22_out);
  and and_37 (and_37_out, or_22_out, not_15_out);
  and and_38 (and_38_out, dipswitch_26_out, not_7_out);
  xor xor_40 (xor_40_out, xor_24_out, or_23_out);
  and and_39 (and_39_out, or_23_out, not_16_out);
  and and_40 (and_40_out, dipswitch_25_out, not_8_out);
  or or_9 (or_9_out, and_9_out, and_10_out);
  or or_10 (or_10_out, and_11_out, and_12_out);
  or or_11 (or_11_out, and_13_out, and_14_out);
  or or_12 (or_12_out, and_15_out, and_16_out);
  or or_13 (or_13_out, and_17_out, and_18_out);
  or or_14 (or_14_out, and_19_out, and_20_out);
  or or_15 (or_15_out, and_21_out, and_22_out);
  or or_16 (or_16_out, and_23_out, and_24_out);
  or or_17 (or_17_out, and_25_out, and_26_out);
  or or_18 (or_18_out, and_27_out, and_28_out);
  or or_19 (or_19_out, and_29_out, and_30_out);
  or or_20 (or_20_out, and_31_out, and_32_out);
  or or_21 (or_21_out, and_33_out, and_34_out);
  or or_22 (or_22_out, and_35_out, and_36_out);
  or or_23 (or_23_out, and_37_out, and_38_out);
  or or_24 (or_24_out, and_39_out, and_40_out);
  or or_25 (or_25_out, dipswitch_1_out, dipswitch_3_out);
  or or_26 (or_26_out, or_25_out, dipswitch_5_out);
  or or_27 (or_27_out, dipswitch_2_out, dipswitch_3_out);
  or or_28 (or_28_out, dipswitch_4_out, dipswitch_5_out);
  or or_29 (or_29_out, or_27_out, dipswitch_6_out);
  or or_30 (or_30_out, or_28_out, dipswitch_6_out);
  or or_31 (or_31_out, dipswitch_8_out, dipswitch_9_out);
  or or_32 (or_32_out, or_26_out, dipswitch_7_out);
  or or_33 (or_33_out, or_29_out, dipswitch_7_out);
  or or_34 (or_34_out, or_32_out, dipswitch_9_out);
  or or_35 (or_35_out, or_30_out, dipswitch_7_out);
  not not_17 (not_17_out, or_35_out);
  not not_18 (not_18_out, or_31_out);
  not not_19 (not_19_out, or_61_out);
  not not_20 (not_20_out, or_61_out);
  not not_21 (not_21_out, or_61_out);
  not not_22 (not_22_out, or_61_out);
  not not_23 (not_23_out, or_61_out);
  not not_24 (not_24_out, or_61_out);
  not not_25 (not_25_out, or_61_out);
  not not_26 (not_26_out, or_61_out);
  not not_27 (not_27_out, or_61_out);
  not not_28 (not_28_out, or_61_out);
  not not_29 (not_29_out, or_61_out);
  not not_30 (not_30_out, or_61_out);
  not not_31 (not_31_out, or_61_out);
  not not_32 (not_32_out, or_61_out);
  not not_33 (not_33_out, or_61_out);
  not not_34 (not_34_out, or_61_out);
  not not_35 (not_35_out, or_34_out);
  not not_36 (not_36_out, or_33_out);
  and and_41 (and_41_out, xor_25_out, not_19_out);
  and and_42 (and_42_out, or_61_out, xor_33_out);
  and and_43 (and_43_out, xor_26_out, not_20_out);
  and and_44 (and_44_out, or_61_out, xor_34_out);
  and and_45 (and_45_out, xor_27_out, not_21_out);
  and and_46 (and_46_out, or_61_out, xor_35_out);
  and and_47 (and_47_out, xor_28_out, not_22_out);
  and and_48 (and_48_out, or_61_out, xor_36_out);
  and and_49 (and_49_out, xor_29_out, not_23_out);
  and and_50 (and_50_out, or_61_out, xor_37_out);
  and and_51 (and_51_out, xor_30_out, not_24_out);
  and and_52 (and_52_out, or_61_out, xor_38_out);
  and and_53 (and_53_out, xor_31_out, not_25_out);
  and and_54 (and_54_out, or_61_out, xor_39_out);
  and and_55 (and_55_out, xor_32_out, not_26_out);
  and and_56 (and_56_out, or_61_out, xor_40_out);
  and and_57 (and_57_out, xor_8_out, not_27_out);
  and and_58 (and_58_out, or_61_out, or_8_out);
  and and_59 (and_59_out, xor_7_out, not_28_out);
  and and_60 (and_60_out, or_61_out, or_7_out);
  and and_61 (and_61_out, xor_6_out, not_29_out);
  and and_62 (and_62_out, or_61_out, or_6_out);
  and and_63 (and_63_out, xor_5_out, not_30_out);
  and and_64 (and_64_out, or_61_out, or_5_out);
  and and_65 (and_65_out, xor_4_out, not_31_out);
  and and_66 (and_66_out, or_61_out, or_4_out);
  and and_67 (and_67_out, xor_3_out, not_32_out);
  and and_68 (and_68_out, or_61_out, or_3_out);
  and and_69 (and_69_out, xor_2_out, not_33_out);
  and and_70 (and_70_out, or_61_out, or_2_out);
  and and_71 (and_71_out, xor_1_out, not_34_out);
  and and_72 (and_72_out, or_61_out, or_1_out);
  and and_73 (and_73_out, not_18_out, not_17_out);
  and and_74 (and_74_out, not_18_out, not_17_out);
  and and_75 (and_75_out, not_18_out, not_17_out);
  and and_76 (and_76_out, not_18_out, not_17_out);
  and and_77 (and_77_out, not_18_out, or_35_out);
  and and_78 (and_78_out, not_18_out, or_35_out);
  and and_79 (and_79_out, not_18_out, or_35_out);
  and and_80 (and_80_out, not_18_out, or_35_out);
  and and_81 (and_81_out, or_31_out, not_17_out);
  and and_82 (and_82_out, or_31_out, not_17_out);
  and and_83 (and_83_out, or_31_out, not_17_out);
  and and_84 (and_84_out, or_31_out, not_17_out);
  and and_85 (and_85_out, or_31_out, or_35_out);
  and and_86 (and_86_out, or_31_out, or_35_out);
  and and_87 (and_87_out, or_31_out, or_35_out);
  and and_88 (and_88_out, or_31_out, or_35_out);
  and and_89 (and_89_out, and_73_out, not_36_out);
  and and_90 (and_90_out, and_74_out, not_36_out);
  and and_91 (and_91_out, and_75_out, or_33_out);
  and and_92 (and_92_out, and_76_out, or_33_out);
  and and_93 (and_93_out, and_77_out, not_36_out);
  and and_94 (and_94_out, and_78_out, not_36_out);
  and and_95 (and_95_out, and_79_out, or_33_out);
  and and_96 (and_96_out, and_80_out, or_33_out);
  and and_97 (and_97_out, and_81_out, not_36_out);
  and and_98 (and_98_out, and_82_out, not_36_out);
  and and_99 (and_99_out, and_83_out, or_33_out);
  and and_100 (and_100_out, and_84_out, or_33_out);
  and and_101 (and_101_out, and_85_out, not_36_out);
  and and_102 (and_102_out, and_86_out, not_36_out);
  and and_103 (and_103_out, and_87_out, or_33_out);
  and and_104 (and_104_out, and_88_out, or_33_out);
  or or_36 (or_36_out, and_41_out, and_42_out);
  or or_37 (or_37_out, and_43_out, and_44_out);
  or or_38 (or_38_out, and_45_out, and_46_out);
  or or_39 (or_39_out, and_47_out, and_48_out);
  or or_40 (or_40_out, and_49_out, and_50_out);
  or or_41 (or_41_out, and_51_out, and_52_out);
  or or_42 (or_42_out, and_53_out, and_54_out);
  or or_43 (or_43_out, and_55_out, and_56_out);
  or or_44 (or_44_out, and_57_out, and_58_out);
  or or_45 (or_45_out, and_59_out, and_60_out);
  or or_46 (or_46_out, and_61_out, and_62_out);
  or or_47 (or_47_out, and_63_out, and_64_out);
  or or_48 (or_48_out, and_65_out, and_66_out);
  or or_49 (or_49_out, and_67_out, and_68_out);
  or or_50 (or_50_out, and_69_out, and_70_out);
  or or_51 (or_51_out, and_71_out, and_72_out);
  // And and_105 has open pins: In_1=and_89_out, In_2=not_35_out, out=open
  and and_106 (and_106_out, and_90_out, or_34_out);
  and and_107 (and_107_out, and_91_out, not_35_out);
  and and_108 (and_108_out, and_92_out, or_34_out);
  and and_109 (and_109_out, and_93_out, not_35_out);
  // And and_110 has open pins: In_1=and_94_out, In_2=or_34_out, out=open
  and and_111 (and_111_out, and_95_out, not_35_out);
  // And and_112 has open pins: In_1=and_96_out, In_2=or_34_out, out=open
  and and_113 (and_113_out, and_97_out, not_35_out);
  and and_114 (and_114_out, and_98_out, or_34_out);
  and and_115 (and_115_out, and_99_out, not_35_out);
  and and_116 (and_116_out, and_100_out, or_34_out);
  and and_117 (and_117_out, and_101_out, not_35_out);
  and and_118 (and_118_out, and_102_out, or_34_out);
  and and_119 (and_119_out, and_103_out, not_35_out);
  and and_120 (and_120_out, and_104_out, or_34_out);
  DipSwitch dipswitch_10 (.out(dipswitch_10_out));
  DipSwitch dipswitch_11 (.out(dipswitch_11_out));
  DipSwitch dipswitch_12 (.out(dipswitch_12_out));
  DipSwitch dipswitch_13 (.out(dipswitch_13_out));
  DipSwitch dipswitch_14 (.out(dipswitch_14_out));
  DipSwitch dipswitch_15 (.out(dipswitch_10_out));
  DipSwitch dipswitch_16 (.out(dipswitch_16_out));
  and and_121 (and_121_out, or_43_out, not_37_out);
  not not_37 (not_37_out, or_60_out);
  and and_122 (and_122_out, or_60_out, or_44_out);
  and and_123 (and_123_out, or_42_out, not_38_out);
  not not_38 (not_38_out, or_60_out);
  and and_124 (and_124_out, or_60_out, or_45_out);
  and and_125 (and_125_out, or_41_out, not_39_out);
  not not_39 (not_39_out, or_60_out);
  and and_126 (and_126_out, or_60_out, or_46_out);
  and and_127 (and_127_out, or_40_out, not_40_out);
  not not_40 (not_40_out, or_60_out);
  and and_128 (and_128_out, or_60_out, or_47_out);
  and and_129 (and_129_out, or_39_out, not_41_out);
  not not_41 (not_41_out, or_60_out);
  and and_130 (and_130_out, or_60_out, or_48_out);
  and and_131 (and_131_out, or_38_out, not_42_out);
  not not_42 (not_42_out, or_60_out);
  and and_132 (and_132_out, or_60_out, or_49_out);
  and and_133 (and_133_out, or_37_out, not_43_out);
  not not_43 (not_43_out, or_60_out);
  and and_134 (and_134_out, or_60_out, or_50_out);
  and and_135 (and_135_out, or_36_out, not_44_out);
  not not_44 (not_44_out, or_60_out);
  and and_136 (and_136_out, or_60_out, or_51_out);
  LED led_1 (.in(or_128_out));
  LED led_2 (.in(or_120_out));
  LED led_3 (.in(or_116_out));
  LED led_4 (.in(or_108_out));
  or or_52 (or_52_out, and_121_out, and_122_out);
  or or_53 (or_53_out, and_123_out, and_124_out);
  or or_54 (or_54_out, and_125_out, and_126_out);
  or or_55 (or_55_out, and_127_out, and_128_out);
  or or_56 (or_56_out, and_129_out, and_130_out);
  or or_57 (or_57_out, and_131_out, and_132_out);
  or or_58 (or_58_out, and_133_out, and_134_out);
  or or_59 (or_59_out, and_135_out, and_136_out);
  LED led_5 (.in(or_104_out));
  LED led_6 (.in(or_96_out));
  LED led_7 (.in(or_92_out));
  LED led_8 (.in(or_84_out));
  not not_45 (not_45_out, and_109_out);
  not not_46 (not_46_out, and_109_out);
  not not_47 (not_47_out, and_109_out);
  not not_48 (not_48_out, and_109_out);
  not not_49 (not_49_out, and_109_out);
  not not_50 (not_50_out, and_109_out);
  not not_51 (not_51_out, and_109_out);
  not not_52 (not_52_out, and_109_out);
  and and_137 (and_137_out, or_52_out, not_45_out);
  and and_138 (and_138_out, and_109_out, and_8_out);
  and and_139 (and_139_out, or_53_out, not_46_out);
  and and_140 (and_140_out, and_109_out, and_7_out);
  and and_141 (and_141_out, or_54_out, not_47_out);
  and and_142 (and_142_out, and_109_out, and_6_out);
  and and_143 (and_143_out, or_55_out, not_48_out);
  and and_144 (and_144_out, and_109_out, and_5_out);
  and and_145 (and_145_out, or_56_out, not_49_out);
  and and_146 (and_146_out, and_109_out, and_4_out);
  and and_147 (and_147_out, or_57_out, not_50_out);
  and and_148 (and_148_out, and_109_out, and_3_out);
  and and_149 (and_149_out, or_58_out, not_51_out);
  and and_150 (and_150_out, and_109_out, and_2_out);
  and and_151 (and_151_out, or_59_out, not_52_out);
  and and_152 (and_152_out, and_109_out, and_1_out);
  or or_60 (or_60_out, and_107_out, and_108_out);
  or or_61 (or_61_out, and_106_out, and_108_out);
  or or_62 (or_62_out, and_137_out, and_138_out);
  or or_63 (or_63_out, and_139_out, and_140_out);
  or or_64 (or_64_out, and_141_out, and_142_out);
  or or_65 (or_65_out, and_143_out, and_144_out);
  or or_66 (or_66_out, and_145_out, and_146_out);
  or or_67 (or_67_out, and_147_out, and_148_out);
  or or_68 (or_68_out, and_149_out, and_150_out);
  or or_69 (or_69_out, and_151_out, and_152_out);
  or or_70 (or_70_out, and_114_out, and_106_out);
  or or_71 (or_71_out, and_107_out, and_108_out);
  or or_72 (or_72_out, and_108_out, and_109_out);
  or or_73 (or_73_out, or_70_out, or_71_out);
  or or_74 (or_74_out, or_71_out, or_72_out);
  or or_75 (or_75_out, or_73_out, or_74_out);
  nand nand_1 (nand_1_out, or_69_out, or_75_out);
  nand nand_2 (nand_2_out, or_68_out, or_75_out);
  nand nand_3 (nand_3_out, or_67_out, or_75_out);
  nand nand_4 (nand_4_out, or_66_out, or_75_out);
  nand nand_5 (nand_5_out, or_65_out, or_75_out);
  nand nand_6 (nand_6_out, or_64_out, or_75_out);
  nand nand_7 (nand_7_out, or_63_out, or_75_out);
  nand nand_8 (nand_8_out, or_62_out, or_75_out);
  nand nand_9 (nand_9_out, nand_1_out, or_75_out);
  nand nand_10 (nand_10_out, nand_2_out, or_75_out);
  nand nand_11 (nand_11_out, nand_3_out, or_75_out);
  nand nand_12 (nand_12_out, nand_4_out, or_75_out);
  nand nand_13 (nand_13_out, nand_5_out, or_75_out);
  nand nand_14 (nand_14_out, nand_6_out, or_75_out);
  nand nand_15 (nand_15_out, nand_7_out, or_75_out);
  nand nand_16 (nand_16_out, nand_8_out, or_75_out);
  nand nand_17 (nand_17_out, nand_1_out, nand_18_out);
  nand nand_18 (nand_18_out, nand_17_out, nand_9_out);
  nand nand_19 (nand_19_out, nand_2_out, nand_20_out);
  nand nand_20 (nand_20_out, nand_19_out, nand_10_out);
  nand nand_21 (nand_21_out, nand_3_out, nand_22_out);
  nand nand_22 (nand_22_out, nand_21_out, nand_11_out);
  nand nand_23 (nand_23_out, nand_4_out, nand_24_out);
  nand nand_24 (nand_24_out, nand_23_out, nand_12_out);
  nand nand_25 (nand_25_out, nand_5_out, nand_26_out);
  nand nand_26 (nand_26_out, nand_25_out, nand_13_out);
  nand nand_27 (nand_27_out, nand_6_out, nand_28_out);
  nand nand_28 (nand_28_out, nand_27_out, nand_14_out);
  nand nand_29 (nand_29_out, nand_7_out, nand_30_out);
  nand nand_30 (nand_30_out, nand_29_out, nand_15_out);
  nand nand_31 (nand_31_out, nand_8_out, nand_32_out);
  nand nand_32 (nand_32_out, nand_31_out, nand_16_out);
  DipSwitch dipswitch_17 (.out(dipswitch_17_out));
  DipSwitch dipswitch_18 (.out(dipswitch_18_out));
  DipSwitch dipswitch_19 (.out(dipswitch_19_out));
  DipSwitch dipswitch_20 (.out(dipswitch_20_out));
  DipSwitch dipswitch_21 (.out(dipswitch_21_out));
  DipSwitch dipswitch_22 (.out(dipswitch_22_out));
  DipSwitch dipswitch_23 (.out(dipswitch_23_out));
  DipSwitch dipswitch_24 (.out(dipswitch_24_out));
  DipSwitch dipswitch_25 (.out(dipswitch_25_out));
  DipSwitch dipswitch_26 (.out(dipswitch_26_out));
  DipSwitch dipswitch_27 (.out(dipswitch_27_out));
  DipSwitch dipswitch_28 (.out(dipswitch_28_out));
  DipSwitch dipswitch_29 (.out(dipswitch_29_out));
  DipSwitch dipswitch_30 (.out(dipswitch_30_out));
  DipSwitch dipswitch_31 (.out(dipswitch_31_out));
  DipSwitch dipswitch_32 (.out(dipswitch_32_out));
  not not_53 (not_53_out, dipswitch_13_out);
  or or_76 (or_76_out, dipswitch_16_out, dipswitch_14_out);
  or or_77 (or_77_out, or_79_out, or_76_out);
  not not_54 (not_54_out, dipswitch_10_out);
  not not_55 (not_55_out, or_77_out);
  or or_78 (dipswitch_10_out, dipswitch_11_out, dipswitch_14_out);
  and and_153 (and_153_out, not_53_out, not_54_out);
  and and_154 (and_154_out, not_53_out, not_54_out);
  and and_155 (and_155_out, not_53_out, dipswitch_10_out);
  and and_156 (and_156_out, not_53_out, dipswitch_10_out);
  and and_157 (and_157_out, dipswitch_13_out, not_54_out);
  and and_158 (and_158_out, dipswitch_13_out, not_54_out);
  and and_159 (and_159_out, dipswitch_13_out, dipswitch_10_out);
  and and_160 (and_160_out, dipswitch_13_out, dipswitch_10_out);
  or or_79 (or_79_out, dipswitch_10_out, dipswitch_12_out);
  or or_80 (dipswitch_13_out, dipswitch_10_out, dipswitch_11_out);
  // And and_161 has open pins: In_1=and_153_out, In_2=not_55_out, out=open
  and and_162 (and_162_out, and_154_out, or_77_out);
  and and_163 (and_163_out, and_155_out, not_55_out);
  and and_164 (and_164_out, and_156_out, or_77_out);
  and and_165 (and_165_out, and_157_out, not_55_out);
  and and_166 (and_166_out, and_158_out, or_77_out);
  and and_167 (and_167_out, and_159_out, not_55_out);
  and and_168 (and_168_out, and_160_out, or_77_out);
  not not_56 (not_56_out, nand_17_out);
  not not_57 (not_57_out, nand_17_out);
  not not_58 (not_58_out, nand_17_out);
  not not_59 (not_59_out, nand_17_out);
  not not_60 (not_60_out, nand_17_out);
  not not_61 (not_61_out, nand_17_out);
  not not_62 (not_62_out, nand_17_out);
  and and_169 (and_169_out, and_162_out, not_56_out);
  and and_170 (and_170_out, and_162_out, nand_17_out);
  and and_171 (and_171_out, and_163_out, not_57_out);
  and and_172 (and_172_out, and_163_out, nand_17_out);
  and and_173 (and_173_out, and_164_out, not_58_out);
  and and_174 (and_174_out, and_164_out, nand_17_out);
  and and_175 (and_175_out, and_165_out, not_59_out);
  and and_176 (and_176_out, and_165_out, nand_17_out);
  and and_177 (and_177_out, and_166_out, not_60_out);
  and and_178 (and_178_out, and_166_out, nand_17_out);
  and and_179 (and_179_out, and_167_out, not_61_out);
  and and_180 (and_180_out, and_167_out, nand_17_out);
  and and_181 (and_181_out, and_168_out, not_62_out);
  and and_182 (and_182_out, and_168_out, nand_17_out);
  not not_63 (not_63_out, and_113_out);
  not not_64 (not_64_out, and_113_out);
  not not_65 (not_65_out, and_113_out);
  not not_66 (not_66_out, and_113_out);
  not not_67 (not_67_out, and_113_out);
  not not_68 (not_68_out, and_113_out);
  not not_69 (not_69_out, and_113_out);
  and and_183 (and_183_out, and_169_out, not_63_out);
  and and_184 (and_184_out, and_170_out, not_63_out);
  and and_185 (and_185_out, and_171_out, not_64_out);
  and and_186 (and_186_out, and_172_out, not_64_out);
  and and_187 (and_187_out, and_173_out, not_65_out);
  and and_188 (and_188_out, and_174_out, not_65_out);
  and and_189 (and_189_out, and_175_out, not_66_out);
  and and_190 (and_190_out, and_176_out, not_66_out);
  and and_191 (and_191_out, and_177_out, not_67_out);
  and and_192 (and_192_out, and_178_out, not_67_out);
  and and_193 (and_193_out, and_179_out, not_68_out);
  and and_194 (and_194_out, and_180_out, not_68_out);
  and and_195 (and_195_out, and_181_out, not_69_out);
  and and_196 (and_196_out, and_182_out, not_69_out);
  nor nor_1 (nor_1_out, and_183_out, nor_2_out);
  nor nor_2 (nor_2_out, nor_1_out, and_184_out);
  nor nor_3 (nor_3_out, and_185_out, nor_4_out);
  nor nor_4 (nor_4_out, nor_3_out, and_186_out);
  nor nor_5 (nor_5_out, and_187_out, nor_6_out);
  nor nor_6 (nor_6_out, nor_5_out, and_188_out);
  nor nor_7 (nor_7_out, and_189_out, nor_8_out);
  nor nor_8 (nor_8_out, nor_7_out, and_190_out);
  nor nor_9 (nor_9_out, and_191_out, nor_10_out);
  nor nor_10 (nor_10_out, nor_9_out, and_192_out);
  nor nor_11 (nor_11_out, and_193_out, nor_12_out);
  nor nor_12 (nor_12_out, nor_11_out, and_194_out);
  nor nor_13 (nor_13_out, and_195_out, nor_14_out);
  nor nor_14 (nor_14_out, nor_13_out, and_196_out);
  and and_197 (and_197_out, and_162_out, nor_1_out);
  and and_198 (and_198_out, and_163_out, nor_3_out);
  and and_199 (and_199_out, and_164_out, nor_5_out);
  and and_200 (and_200_out, and_165_out, nor_7_out);
  and and_201 (and_201_out, and_166_out, nor_9_out);
  and and_202 (and_202_out, and_167_out, nor_11_out);
  and and_203 (and_203_out, and_168_out, nor_13_out);
  and and_204 (and_204_out, and_197_out, and_113_out);
  and and_205 (and_205_out, and_198_out, and_113_out);
  and and_206 (and_206_out, and_199_out, and_113_out);
  and and_207 (and_207_out, and_200_out, and_113_out);
  and and_208 (and_208_out, and_201_out, and_113_out);
  and and_209 (and_209_out, and_202_out, and_113_out);
  and and_210 (and_210_out, and_203_out, and_113_out);
  or or_81 (or_81_out, and_208_out, and_210_out);
  or or_82 (or_82_out, and_209_out, or_81_out);
  or or_83 (or_83_out, and_207_out, or_82_out);
  or or_84 (or_84_out, or_86_out, or_83_out);
  or or_85 (or_85_out, and_205_out, and_206_out);
  or or_86 (or_86_out, and_204_out, or_85_out);
  not not_70 (not_70_out, nand_19_out);
  not not_71 (not_71_out, nand_19_out);
  not not_72 (not_72_out, nand_19_out);
  not not_73 (not_73_out, nand_19_out);
  not not_74 (not_74_out, nand_19_out);
  not not_75 (not_75_out, nand_19_out);
  not not_76 (not_76_out, nand_19_out);
  and and_211 (and_211_out, and_162_out, not_70_out);
  and and_212 (and_212_out, and_162_out, nand_19_out);
  and and_213 (and_213_out, and_163_out, not_71_out);
  and and_214 (and_214_out, and_163_out, nand_19_out);
  and and_215 (and_215_out, and_164_out, not_72_out);
  and and_216 (and_216_out, and_164_out, nand_19_out);
  and and_217 (and_217_out, and_165_out, not_73_out);
  and and_218 (and_218_out, and_165_out, nand_19_out);
  and and_219 (and_219_out, and_166_out, not_74_out);
  and and_220 (and_220_out, and_166_out, nand_19_out);
  and and_221 (and_221_out, and_167_out, not_75_out);
  and and_222 (and_222_out, and_167_out, nand_19_out);
  and and_223 (and_223_out, and_168_out, not_76_out);
  and and_224 (and_224_out, and_168_out, nand_19_out);
  and and_225 (and_225_out, and_211_out, not_77_out);
  and and_226 (and_226_out, and_212_out, not_77_out);
  not not_77 (not_77_out, and_113_out);
  and and_227 (and_227_out, and_213_out, not_78_out);
  and and_228 (and_228_out, and_214_out, not_78_out);
  not not_78 (not_78_out, and_113_out);
  and and_229 (and_229_out, and_215_out, not_79_out);
  and and_230 (and_230_out, and_216_out, not_79_out);
  not not_79 (not_79_out, and_113_out);
  and and_231 (and_231_out, and_217_out, not_80_out);
  and and_232 (and_232_out, and_218_out, not_80_out);
  not not_80 (not_80_out, and_113_out);
  and and_233 (and_233_out, and_219_out, not_81_out);
  and and_234 (and_234_out, and_220_out, not_81_out);
  not not_81 (not_81_out, and_113_out);
  and and_235 (and_235_out, and_221_out, not_82_out);
  and and_236 (and_236_out, and_222_out, not_82_out);
  not not_82 (not_82_out, and_113_out);
  and and_237 (and_237_out, and_223_out, not_83_out);
  and and_238 (and_238_out, and_224_out, not_83_out);
  not not_83 (not_83_out, and_113_out);
  nor nor_15 (nor_15_out, and_225_out, nor_16_out);
  nor nor_16 (nor_16_out, nor_15_out, and_226_out);
  nor nor_17 (nor_17_out, and_227_out, nor_18_out);
  nor nor_18 (nor_18_out, nor_17_out, and_228_out);
  nor nor_19 (nor_19_out, and_229_out, nor_20_out);
  nor nor_20 (nor_20_out, nor_19_out, and_230_out);
  nor nor_21 (nor_21_out, and_231_out, nor_22_out);
  nor nor_22 (nor_22_out, nor_21_out, and_232_out);
  nor nor_23 (nor_23_out, and_233_out, nor_24_out);
  nor nor_24 (nor_24_out, nor_23_out, and_234_out);
  nor nor_25 (nor_25_out, and_235_out, nor_26_out);
  nor nor_26 (nor_26_out, nor_25_out, and_236_out);
  nor nor_27 (nor_27_out, and_237_out, nor_28_out);
  nor nor_28 (nor_28_out, nor_27_out, and_238_out);
  and and_239 (and_239_out, and_162_out, nor_15_out);
  and and_240 (and_240_out, and_163_out, nor_17_out);
  and and_241 (and_241_out, and_164_out, nor_19_out);
  and and_242 (and_242_out, and_165_out, nor_21_out);
  and and_243 (and_243_out, and_166_out, nor_23_out);
  and and_244 (and_244_out, and_167_out, nor_25_out);
  and and_245 (and_245_out, and_168_out, nor_27_out);
  and and_246 (and_246_out, and_239_out, and_113_out);
  and and_247 (and_247_out, and_240_out, and_113_out);
  and and_248 (and_248_out, and_241_out, and_113_out);
  and and_249 (and_249_out, and_242_out, and_113_out);
  and and_250 (and_250_out, and_243_out, and_113_out);
  and and_251 (and_251_out, and_244_out, and_113_out);
  and and_252 (and_252_out, and_245_out, and_113_out);
  or or_87 (or_87_out, and_250_out, and_252_out);
  or or_88 (or_88_out, and_251_out, or_87_out);
  or or_89 (or_89_out, and_249_out, or_88_out);
  or or_90 (or_90_out, and_247_out, and_248_out);
  or or_91 (or_91_out, and_246_out, or_90_out);
  or or_92 (or_92_out, or_91_out, or_89_out);
  not not_84 (not_84_out, nand_21_out);
  not not_85 (not_85_out, nand_21_out);
  not not_86 (not_86_out, nand_21_out);
  not not_87 (not_87_out, nand_21_out);
  not not_88 (not_88_out, nand_21_out);
  not not_89 (not_89_out, nand_21_out);
  not not_90 (not_90_out, nand_21_out);
  and and_253 (and_253_out, and_162_out, not_84_out);
  and and_254 (and_254_out, and_162_out, nand_21_out);
  and and_255 (and_255_out, and_163_out, not_85_out);
  and and_256 (and_256_out, and_163_out, nand_21_out);
  and and_257 (and_257_out, and_164_out, not_86_out);
  and and_258 (and_258_out, and_164_out, nand_21_out);
  and and_259 (and_259_out, and_165_out, not_87_out);
  and and_260 (and_260_out, and_165_out, nand_21_out);
  and and_261 (and_261_out, and_166_out, not_88_out);
  and and_262 (and_262_out, and_166_out, nand_21_out);
  and and_263 (and_263_out, and_167_out, not_89_out);
  and and_264 (and_264_out, and_167_out, nand_21_out);
  and and_265 (and_265_out, and_168_out, not_90_out);
  and and_266 (and_266_out, and_168_out, nand_21_out);
  not not_91 (not_91_out, and_113_out);
  not not_92 (not_92_out, and_113_out);
  not not_93 (not_93_out, and_113_out);
  not not_94 (not_94_out, and_113_out);
  not not_95 (not_95_out, and_113_out);
  not not_96 (not_96_out, and_113_out);
  not not_97 (not_97_out, and_113_out);
  and and_267 (and_267_out, and_253_out, not_91_out);
  and and_268 (and_268_out, and_254_out, not_91_out);
  and and_269 (and_269_out, and_255_out, not_92_out);
  and and_270 (and_270_out, and_256_out, not_92_out);
  and and_271 (and_271_out, and_257_out, not_93_out);
  and and_272 (and_272_out, and_258_out, not_93_out);
  and and_273 (and_273_out, and_259_out, not_94_out);
  and and_274 (and_274_out, and_260_out, not_94_out);
  and and_275 (and_275_out, and_261_out, not_95_out);
  and and_276 (and_276_out, and_262_out, not_95_out);
  and and_277 (and_277_out, and_263_out, not_96_out);
  and and_278 (and_278_out, and_264_out, not_96_out);
  and and_279 (and_279_out, and_265_out, not_97_out);
  and and_280 (and_280_out, and_266_out, not_97_out);
  nor nor_29 (nor_29_out, and_267_out, nor_30_out);
  nor nor_30 (nor_30_out, nor_29_out, and_268_out);
  nor nor_31 (nor_31_out, and_269_out, nor_32_out);
  nor nor_32 (nor_32_out, nor_31_out, and_270_out);
  nor nor_33 (nor_33_out, and_271_out, nor_34_out);
  nor nor_34 (nor_34_out, nor_33_out, and_272_out);
  nor nor_35 (nor_35_out, and_273_out, nor_36_out);
  nor nor_36 (nor_36_out, nor_35_out, and_274_out);
  nor nor_37 (nor_37_out, and_275_out, nor_38_out);
  nor nor_38 (nor_38_out, nor_37_out, and_276_out);
  nor nor_39 (nor_39_out, and_277_out, nor_40_out);
  nor nor_40 (nor_40_out, nor_39_out, and_278_out);
  nor nor_41 (nor_41_out, and_279_out, nor_42_out);
  nor nor_42 (nor_42_out, nor_41_out, and_280_out);
  and and_281 (and_281_out, and_162_out, nor_29_out);
  and and_282 (and_282_out, and_163_out, nor_31_out);
  and and_283 (and_283_out, and_164_out, nor_33_out);
  and and_284 (and_284_out, and_165_out, nor_35_out);
  and and_285 (and_285_out, and_166_out, nor_37_out);
  and and_286 (and_286_out, and_167_out, nor_39_out);
  and and_287 (and_287_out, and_168_out, nor_41_out);
  and and_288 (and_288_out, and_281_out, and_113_out);
  and and_289 (and_289_out, and_282_out, and_113_out);
  and and_290 (and_290_out, and_283_out, and_113_out);
  and and_291 (and_291_out, and_284_out, and_113_out);
  and and_292 (and_292_out, and_285_out, and_113_out);
  and and_293 (and_293_out, and_286_out, and_113_out);
  and and_294 (and_294_out, and_287_out, and_113_out);
  or or_93 (or_93_out, and_292_out, and_294_out);
  or or_94 (or_94_out, and_293_out, or_93_out);
  or or_95 (or_95_out, and_291_out, or_94_out);
  or or_96 (or_96_out, or_98_out, or_95_out);
  or or_97 (or_97_out, and_289_out, and_290_out);
  or or_98 (or_98_out, and_288_out, or_97_out);
  not not_98 (not_98_out, nand_23_out);
  not not_99 (not_99_out, nand_23_out);
  not not_100 (not_100_out, nand_23_out);
  not not_101 (not_101_out, nand_23_out);
  not not_102 (not_102_out, nand_23_out);
  not not_103 (not_103_out, nand_23_out);
  not not_104 (not_104_out, nand_23_out);
  and and_295 (and_295_out, and_162_out, not_98_out);
  and and_296 (and_296_out, and_162_out, nand_23_out);
  and and_297 (and_297_out, and_163_out, not_99_out);
  and and_298 (and_298_out, and_163_out, nand_23_out);
  and and_299 (and_299_out, and_164_out, not_100_out);
  and and_300 (and_300_out, and_164_out, nand_23_out);
  and and_301 (and_301_out, and_165_out, not_101_out);
  and and_302 (and_302_out, and_165_out, nand_23_out);
  and and_303 (and_303_out, and_166_out, not_102_out);
  and and_304 (and_304_out, and_166_out, nand_23_out);
  and and_305 (and_305_out, and_167_out, not_103_out);
  and and_306 (and_306_out, and_167_out, nand_23_out);
  and and_307 (and_307_out, and_168_out, not_104_out);
  and and_308 (and_308_out, and_168_out, nand_23_out);
  and and_309 (and_309_out, and_295_out, not_105_out);
  and and_310 (and_310_out, and_296_out, not_105_out);
  not not_105 (not_105_out, and_113_out);
  and and_311 (and_311_out, and_297_out, not_106_out);
  and and_312 (and_312_out, and_298_out, not_106_out);
  not not_106 (not_106_out, and_113_out);
  and and_313 (and_313_out, and_299_out, not_107_out);
  and and_314 (and_314_out, and_300_out, not_107_out);
  not not_107 (not_107_out, and_113_out);
  and and_315 (and_315_out, and_301_out, not_108_out);
  and and_316 (and_316_out, and_302_out, not_108_out);
  not not_108 (not_108_out, and_113_out);
  and and_317 (and_317_out, and_303_out, not_109_out);
  and and_318 (and_318_out, and_304_out, not_109_out);
  not not_109 (not_109_out, and_113_out);
  and and_319 (and_319_out, and_305_out, not_110_out);
  and and_320 (and_320_out, and_306_out, not_110_out);
  not not_110 (not_110_out, and_113_out);
  and and_321 (and_321_out, and_307_out, not_111_out);
  and and_322 (and_322_out, and_308_out, not_111_out);
  not not_111 (not_111_out, and_113_out);
  nor nor_43 (nor_43_out, and_309_out, nor_44_out);
  nor nor_44 (nor_44_out, nor_43_out, and_310_out);
  nor nor_45 (nor_45_out, and_311_out, nor_46_out);
  nor nor_46 (nor_46_out, nor_45_out, and_312_out);
  nor nor_47 (nor_47_out, and_313_out, nor_48_out);
  nor nor_48 (nor_48_out, nor_47_out, and_314_out);
  nor nor_49 (nor_49_out, and_315_out, nor_50_out);
  nor nor_50 (nor_50_out, nor_49_out, and_316_out);
  nor nor_51 (nor_51_out, and_317_out, nor_52_out);
  nor nor_52 (nor_52_out, nor_51_out, and_318_out);
  nor nor_53 (nor_53_out, and_319_out, nor_54_out);
  nor nor_54 (nor_54_out, nor_53_out, and_320_out);
  nor nor_55 (nor_55_out, and_321_out, nor_56_out);
  nor nor_56 (nor_56_out, nor_55_out, and_322_out);
  and and_323 (and_323_out, and_162_out, nor_43_out);
  and and_324 (and_324_out, and_163_out, nor_45_out);
  and and_325 (and_325_out, and_164_out, nor_47_out);
  and and_326 (and_326_out, and_165_out, nor_49_out);
  and and_327 (and_327_out, and_166_out, nor_51_out);
  and and_328 (and_328_out, and_167_out, nor_53_out);
  and and_329 (and_329_out, and_168_out, nor_55_out);
  and and_330 (and_330_out, and_323_out, and_113_out);
  and and_331 (and_331_out, and_324_out, and_113_out);
  and and_332 (and_332_out, and_325_out, and_113_out);
  and and_333 (and_333_out, and_326_out, and_113_out);
  and and_334 (and_334_out, and_327_out, and_113_out);
  and and_335 (and_335_out, and_328_out, and_113_out);
  and and_336 (and_336_out, and_329_out, and_113_out);
  or or_99 (or_99_out, and_334_out, and_336_out);
  or or_100 (or_100_out, and_335_out, or_99_out);
  or or_101 (or_101_out, and_333_out, or_100_out);
  or or_102 (or_102_out, and_331_out, and_332_out);
  or or_103 (or_103_out, and_330_out, or_102_out);
  or or_104 (or_104_out, or_103_out, or_101_out);
  not not_112 (not_112_out, nand_25_out);
  not not_113 (not_113_out, nand_25_out);
  not not_114 (not_114_out, nand_25_out);
  not not_115 (not_115_out, nand_25_out);
  not not_116 (not_116_out, nand_25_out);
  not not_117 (not_117_out, nand_25_out);
  not not_118 (not_118_out, nand_25_out);
  and and_337 (and_337_out, and_162_out, not_112_out);
  and and_338 (and_338_out, and_162_out, nand_25_out);
  and and_339 (and_339_out, and_163_out, not_113_out);
  and and_340 (and_340_out, and_163_out, nand_25_out);
  and and_341 (and_341_out, and_164_out, not_114_out);
  and and_342 (and_342_out, and_164_out, nand_25_out);
  and and_343 (and_343_out, and_165_out, not_115_out);
  and and_344 (and_344_out, and_165_out, nand_25_out);
  and and_345 (and_345_out, and_166_out, not_116_out);
  and and_346 (and_346_out, and_166_out, nand_25_out);
  and and_347 (and_347_out, and_167_out, not_117_out);
  and and_348 (and_348_out, and_167_out, nand_25_out);
  and and_349 (and_349_out, and_168_out, not_118_out);
  and and_350 (and_350_out, and_168_out, nand_25_out);
  not not_119 (not_119_out, and_113_out);
  not not_120 (not_120_out, and_113_out);
  not not_121 (not_121_out, and_113_out);
  not not_122 (not_122_out, and_113_out);
  not not_123 (not_123_out, and_113_out);
  not not_124 (not_124_out, and_113_out);
  not not_125 (not_125_out, and_113_out);
  and and_351 (and_351_out, and_337_out, not_119_out);
  and and_352 (and_352_out, and_338_out, not_119_out);
  and and_353 (and_353_out, and_339_out, not_120_out);
  and and_354 (and_354_out, and_340_out, not_120_out);
  and and_355 (and_355_out, and_341_out, not_121_out);
  and and_356 (and_356_out, and_342_out, not_121_out);
  and and_357 (and_357_out, and_343_out, not_122_out);
  and and_358 (and_358_out, and_344_out, not_122_out);
  and and_359 (and_359_out, and_345_out, not_123_out);
  and and_360 (and_360_out, and_346_out, not_123_out);
  and and_361 (and_361_out, and_347_out, not_124_out);
  and and_362 (and_362_out, and_348_out, not_124_out);
  and and_363 (and_363_out, and_349_out, not_125_out);
  and and_364 (and_364_out, and_350_out, not_125_out);
  nor nor_57 (nor_57_out, and_351_out, nor_58_out);
  nor nor_58 (nor_58_out, nor_57_out, and_352_out);
  nor nor_59 (nor_59_out, and_353_out, nor_60_out);
  nor nor_60 (nor_60_out, nor_59_out, and_354_out);
  nor nor_61 (nor_61_out, and_355_out, nor_62_out);
  nor nor_62 (nor_62_out, nor_61_out, and_356_out);
  nor nor_63 (nor_63_out, and_357_out, nor_64_out);
  nor nor_64 (nor_64_out, nor_63_out, and_358_out);
  nor nor_65 (nor_65_out, and_359_out, nor_66_out);
  nor nor_66 (nor_66_out, nor_65_out, and_360_out);
  nor nor_67 (nor_67_out, and_361_out, nor_68_out);
  nor nor_68 (nor_68_out, nor_67_out, and_362_out);
  nor nor_69 (nor_69_out, and_363_out, nor_70_out);
  nor nor_70 (nor_70_out, nor_69_out, and_364_out);
  and and_365 (and_365_out, and_162_out, nor_57_out);
  and and_366 (and_366_out, and_163_out, nor_59_out);
  and and_367 (and_367_out, and_164_out, nor_61_out);
  and and_368 (and_368_out, and_165_out, nor_63_out);
  and and_369 (and_369_out, and_166_out, nor_65_out);
  and and_370 (and_370_out, and_167_out, nor_67_out);
  and and_371 (and_371_out, and_168_out, nor_69_out);
  and and_372 (and_372_out, and_365_out, and_113_out);
  and and_373 (and_373_out, and_366_out, and_113_out);
  and and_374 (and_374_out, and_367_out, and_113_out);
  and and_375 (and_375_out, and_368_out, and_113_out);
  and and_376 (and_376_out, and_369_out, and_113_out);
  and and_377 (and_377_out, and_370_out, and_113_out);
  and and_378 (and_378_out, and_371_out, and_113_out);
  or or_105 (or_105_out, and_376_out, and_378_out);
  or or_106 (or_106_out, and_377_out, or_105_out);
  or or_107 (or_107_out, and_375_out, or_106_out);
  or or_108 (or_108_out, or_110_out, or_107_out);
  or or_109 (or_109_out, and_373_out, and_374_out);
  or or_110 (or_110_out, and_372_out, or_109_out);
  not not_126 (not_126_out, nand_27_out);
  not not_127 (not_127_out, nand_27_out);
  not not_128 (not_128_out, nand_27_out);
  not not_129 (not_129_out, nand_27_out);
  not not_130 (not_130_out, nand_27_out);
  not not_131 (not_131_out, nand_27_out);
  not not_132 (not_132_out, nand_27_out);
  and and_379 (and_379_out, and_162_out, not_126_out);
  and and_380 (and_380_out, and_162_out, nand_27_out);
  and and_381 (and_381_out, and_163_out, not_127_out);
  and and_382 (and_382_out, and_163_out, nand_27_out);
  and and_383 (and_383_out, and_164_out, not_128_out);
  and and_384 (and_384_out, and_164_out, nand_27_out);
  and and_385 (and_385_out, and_165_out, not_129_out);
  and and_386 (and_386_out, and_165_out, nand_27_out);
  and and_387 (and_387_out, and_166_out, not_130_out);
  and and_388 (and_388_out, and_166_out, nand_27_out);
  and and_389 (and_389_out, and_167_out, not_131_out);
  and and_390 (and_390_out, and_167_out, nand_27_out);
  and and_391 (and_391_out, and_168_out, not_132_out);
  and and_392 (and_392_out, and_168_out, nand_27_out);
  and and_393 (and_393_out, and_379_out, not_133_out);
  and and_394 (and_394_out, and_380_out, not_133_out);
  not not_133 (not_133_out, and_113_out);
  and and_395 (and_395_out, and_381_out, not_134_out);
  and and_396 (and_396_out, and_382_out, not_134_out);
  not not_134 (not_134_out, and_113_out);
  and and_397 (and_397_out, and_383_out, not_135_out);
  and and_398 (and_398_out, and_384_out, not_135_out);
  not not_135 (not_135_out, and_113_out);
  and and_399 (and_399_out, and_385_out, not_136_out);
  and and_400 (and_400_out, and_386_out, not_136_out);
  not not_136 (not_136_out, and_113_out);
  and and_401 (and_401_out, and_387_out, not_137_out);
  and and_402 (and_402_out, and_388_out, not_137_out);
  not not_137 (not_137_out, and_113_out);
  and and_403 (and_403_out, and_389_out, not_138_out);
  and and_404 (and_404_out, and_390_out, not_138_out);
  not not_138 (not_138_out, and_113_out);
  and and_405 (and_405_out, and_391_out, not_139_out);
  and and_406 (and_406_out, and_392_out, not_139_out);
  not not_139 (not_139_out, and_113_out);
  nor nor_71 (nor_71_out, and_393_out, nor_72_out);
  nor nor_72 (nor_72_out, nor_71_out, and_394_out);
  nor nor_73 (nor_73_out, and_395_out, nor_74_out);
  nor nor_74 (nor_74_out, nor_73_out, and_396_out);
  nor nor_75 (nor_75_out, and_397_out, nor_76_out);
  nor nor_76 (nor_76_out, nor_75_out, and_398_out);
  nor nor_77 (nor_77_out, and_399_out, nor_78_out);
  nor nor_78 (nor_78_out, nor_77_out, and_400_out);
  nor nor_79 (nor_79_out, and_401_out, nor_80_out);
  nor nor_80 (nor_80_out, nor_79_out, and_402_out);
  nor nor_81 (nor_81_out, and_403_out, nor_82_out);
  nor nor_82 (nor_82_out, nor_81_out, and_404_out);
  nor nor_83 (nor_83_out, and_405_out, nor_84_out);
  nor nor_84 (nor_84_out, nor_83_out, and_406_out);
  and and_407 (and_407_out, and_162_out, nor_71_out);
  and and_408 (and_408_out, and_163_out, nor_73_out);
  and and_409 (and_409_out, and_164_out, nor_75_out);
  and and_410 (and_410_out, and_165_out, nor_77_out);
  and and_411 (and_411_out, and_166_out, nor_79_out);
  and and_412 (and_412_out, and_167_out, nor_81_out);
  and and_413 (and_413_out, and_168_out, nor_83_out);
  and and_414 (and_414_out, and_407_out, and_113_out);
  and and_415 (and_415_out, and_408_out, and_113_out);
  and and_416 (and_416_out, and_409_out, and_113_out);
  and and_417 (and_417_out, and_410_out, and_113_out);
  and and_418 (and_418_out, and_411_out, and_113_out);
  and and_419 (and_419_out, and_412_out, and_113_out);
  and and_420 (and_420_out, and_413_out, and_113_out);
  or or_111 (or_111_out, and_418_out, and_420_out);
  or or_112 (or_112_out, and_419_out, or_111_out);
  or or_113 (or_113_out, and_417_out, or_112_out);
  or or_114 (or_114_out, and_415_out, and_416_out);
  or or_115 (or_115_out, and_414_out, or_114_out);
  or or_116 (or_116_out, or_115_out, or_113_out);
  not not_140 (not_140_out, nand_29_out);
  not not_141 (not_141_out, nand_29_out);
  not not_142 (not_142_out, nand_29_out);
  not not_143 (not_143_out, nand_29_out);
  not not_144 (not_144_out, nand_29_out);
  not not_145 (not_145_out, nand_29_out);
  not not_146 (not_146_out, nand_29_out);
  and and_421 (and_421_out, and_162_out, not_140_out);
  and and_422 (and_422_out, and_162_out, nand_29_out);
  and and_423 (and_423_out, and_163_out, not_141_out);
  and and_424 (and_424_out, and_163_out, nand_29_out);
  and and_425 (and_425_out, and_164_out, not_142_out);
  and and_426 (and_426_out, and_164_out, nand_29_out);
  and and_427 (and_427_out, and_165_out, not_143_out);
  and and_428 (and_428_out, and_165_out, nand_29_out);
  and and_429 (and_429_out, and_166_out, not_144_out);
  and and_430 (and_430_out, and_166_out, nand_29_out);
  and and_431 (and_431_out, and_167_out, not_145_out);
  and and_432 (and_432_out, and_167_out, nand_29_out);
  and and_433 (and_433_out, and_168_out, not_146_out);
  and and_434 (and_434_out, and_168_out, nand_29_out);
  not not_147 (not_147_out, and_113_out);
  not not_148 (not_148_out, and_113_out);
  not not_149 (not_149_out, and_113_out);
  not not_150 (not_150_out, and_113_out);
  not not_151 (not_151_out, and_113_out);
  not not_152 (not_152_out, and_113_out);
  not not_153 (not_153_out, and_113_out);
  and and_435 (and_435_out, and_421_out, not_147_out);
  and and_436 (and_436_out, and_422_out, not_147_out);
  and and_437 (and_437_out, and_423_out, not_148_out);
  and and_438 (and_438_out, and_424_out, not_148_out);
  and and_439 (and_439_out, and_425_out, not_149_out);
  and and_440 (and_440_out, and_426_out, not_149_out);
  and and_441 (and_441_out, and_427_out, not_150_out);
  and and_442 (and_442_out, and_428_out, not_150_out);
  and and_443 (and_443_out, and_429_out, not_151_out);
  and and_444 (and_444_out, and_430_out, not_151_out);
  and and_445 (and_445_out, and_431_out, not_152_out);
  and and_446 (and_446_out, and_432_out, not_152_out);
  and and_447 (and_447_out, and_433_out, not_153_out);
  and and_448 (and_448_out, and_434_out, not_153_out);
  nor nor_85 (nor_85_out, and_435_out, nor_86_out);
  nor nor_86 (nor_86_out, nor_85_out, and_436_out);
  nor nor_87 (nor_87_out, and_437_out, nor_88_out);
  nor nor_88 (nor_88_out, nor_87_out, and_438_out);
  nor nor_89 (nor_89_out, and_439_out, nor_90_out);
  nor nor_90 (nor_90_out, nor_89_out, and_440_out);
  nor nor_91 (nor_91_out, and_441_out, nor_92_out);
  nor nor_92 (nor_92_out, nor_91_out, and_442_out);
  nor nor_93 (nor_93_out, and_443_out, nor_94_out);
  nor nor_94 (nor_94_out, nor_93_out, and_444_out);
  nor nor_95 (nor_95_out, and_445_out, nor_96_out);
  nor nor_96 (nor_96_out, nor_95_out, and_446_out);
  nor nor_97 (nor_97_out, and_447_out, nor_98_out);
  nor nor_98 (nor_98_out, nor_97_out, and_448_out);
  and and_449 (and_449_out, and_162_out, nor_85_out);
  and and_450 (and_450_out, and_163_out, nor_87_out);
  and and_451 (and_451_out, and_164_out, nor_89_out);
  and and_452 (and_452_out, and_165_out, nor_91_out);
  and and_453 (and_453_out, and_166_out, nor_93_out);
  and and_454 (and_454_out, and_167_out, nor_95_out);
  and and_455 (and_455_out, and_168_out, nor_97_out);
  and and_456 (and_456_out, and_449_out, and_113_out);
  and and_457 (and_457_out, and_450_out, and_113_out);
  and and_458 (and_458_out, and_451_out, and_113_out);
  and and_459 (and_459_out, and_452_out, and_113_out);
  and and_460 (and_460_out, and_453_out, and_113_out);
  and and_461 (and_461_out, and_454_out, and_113_out);
  and and_462 (and_462_out, and_455_out, and_113_out);
  or or_117 (or_117_out, and_460_out, and_462_out);
  or or_118 (or_118_out, and_461_out, or_117_out);
  or or_119 (or_119_out, and_459_out, or_118_out);
  or or_120 (or_120_out, or_122_out, or_119_out);
  or or_121 (or_121_out, and_457_out, and_458_out);
  or or_122 (or_122_out, and_456_out, or_121_out);
  not not_154 (not_154_out, nand_31_out);
  not not_155 (not_155_out, nand_31_out);
  not not_156 (not_156_out, nand_31_out);
  not not_157 (not_157_out, nand_31_out);
  not not_158 (not_158_out, nand_31_out);
  not not_159 (not_159_out, nand_31_out);
  not not_160 (not_160_out, nand_31_out);
  and and_463 (and_463_out, and_162_out, not_154_out);
  and and_464 (and_464_out, and_162_out, nand_31_out);
  and and_465 (and_465_out, and_163_out, not_155_out);
  and and_466 (and_466_out, and_163_out, nand_31_out);
  and and_467 (and_467_out, and_164_out, not_156_out);
  and and_468 (and_468_out, and_164_out, nand_31_out);
  and and_469 (and_469_out, and_165_out, not_157_out);
  and and_470 (and_470_out, and_165_out, nand_31_out);
  and and_471 (and_471_out, and_166_out, not_158_out);
  and and_472 (and_472_out, and_166_out, nand_31_out);
  and and_473 (and_473_out, and_167_out, not_159_out);
  and and_474 (and_474_out, and_167_out, nand_31_out);
  and and_475 (and_475_out, and_168_out, not_160_out);
  and and_476 (and_476_out, and_168_out, nand_31_out);
  and and_477 (and_477_out, and_463_out, not_161_out);
  and and_478 (and_478_out, and_464_out, not_161_out);
  not not_161 (not_161_out, and_113_out);
  and and_479 (and_479_out, and_465_out, not_162_out);
  and and_480 (and_480_out, and_466_out, not_162_out);
  not not_162 (not_162_out, and_113_out);
  and and_481 (and_481_out, and_467_out, not_163_out);
  and and_482 (and_482_out, and_468_out, not_163_out);
  not not_163 (not_163_out, and_113_out);
  and and_483 (and_483_out, and_469_out, not_164_out);
  and and_484 (and_484_out, and_470_out, not_164_out);
  not not_164 (not_164_out, and_113_out);
  and and_485 (and_485_out, and_471_out, not_165_out);
  and and_486 (and_486_out, and_472_out, not_165_out);
  not not_165 (not_165_out, and_113_out);
  and and_487 (and_487_out, and_473_out, not_166_out);
  and and_488 (and_488_out, and_474_out, not_166_out);
  not not_166 (not_166_out, and_113_out);
  and and_489 (and_489_out, and_475_out, not_167_out);
  and and_490 (and_490_out, and_476_out, not_167_out);
  not not_167 (not_167_out, and_113_out);
  nor nor_99 (nor_99_out, and_477_out, nor_100_out);
  nor nor_100 (nor_100_out, nor_99_out, and_478_out);
  nor nor_101 (nor_101_out, and_479_out, nor_102_out);
  nor nor_102 (nor_102_out, nor_101_out, and_480_out);
  nor nor_103 (nor_103_out, and_481_out, nor_104_out);
  nor nor_104 (nor_104_out, nor_103_out, and_482_out);
  nor nor_105 (nor_105_out, and_483_out, nor_106_out);
  nor nor_106 (nor_106_out, nor_105_out, and_484_out);
  nor nor_107 (nor_107_out, and_485_out, nor_108_out);
  nor nor_108 (nor_108_out, nor_107_out, and_486_out);
  nor nor_109 (nor_109_out, and_487_out, nor_110_out);
  nor nor_110 (nor_110_out, nor_109_out, and_488_out);
  nor nor_111 (nor_111_out, and_489_out, nor_112_out);
  nor nor_112 (nor_112_out, nor_111_out, and_490_out);
  and and_491 (and_491_out, and_162_out, nor_99_out);
  and and_492 (and_492_out, and_163_out, nor_101_out);
  and and_493 (and_493_out, and_164_out, nor_103_out);
  and and_494 (and_494_out, and_165_out, nor_105_out);
  and and_495 (and_495_out, and_166_out, nor_107_out);
  and and_496 (and_496_out, and_167_out, nor_109_out);
  and and_497 (and_497_out, and_168_out, nor_111_out);
  and and_498 (and_498_out, and_491_out, and_113_out);
  and and_499 (and_499_out, and_492_out, and_113_out);
  and and_500 (and_500_out, and_493_out, and_113_out);
  and and_501 (and_501_out, and_494_out, and_113_out);
  and and_502 (and_502_out, and_495_out, and_113_out);
  and and_503 (and_503_out, and_496_out, and_113_out);
  and and_504 (and_504_out, and_497_out, and_113_out);
  or or_123 (or_123_out, and_502_out, and_504_out);
  or or_124 (or_124_out, and_503_out, or_123_out);
  or or_125 (or_125_out, and_501_out, or_124_out);
  or or_126 (or_126_out, and_499_out, and_500_out);
  or or_127 (or_127_out, and_498_out, or_126_out);
  or or_128 (or_128_out, or_127_out, or_125_out);

  // Notes on the sheet:
  //   A XOR B
  //   A AND B
  //   WRITE/READ
  //   CLOCK CACHE
  //   SUB
  //   A OR B
  //   MOVE
  //   CLEAR
  //   0000 - ADD
  //   0001 - SUB
  //   0010 - A XOR B
  //   0011 - A OR B
  //   0100 - A AND B
  //   0101 - MOVE
  //   0110 - CLEAR
  //   0111 - READ
  //   1000 - WRITE
  //   1001 - CLOCK CACHE
endmodule
