// Digital circuit 3 to 8 line decoder.dig as structural Verilog
module _3_to_8_line_decoder (
);

  wire and_1_out, and_2_out, and_3_out, and_4_out, and_5_out, and_6_out, and_7_out, and_8_out, and_9_out,
       and_10_out, and_11_out, and_12_out, and_13_out, and_14_out, and_15_out, and_16_out, not_1_out,
       not_2_out, not_3_out, undriven, undriven_2, undriven_3;

  not not_1 (not_1_out, undriven);
  not not_2 (not_2_out, undriven_2);
  not not_3 (not_3_out, undriven_3);
  and and_1 (and_1_out, not_1_out, not_2_out);
  and and_2 (and_2_out, not_1_out, not_2_out);
  and and_3 (and_3_out, not_1_out, undriven_2);
  and and_4 (and_4_out, not_1_out, undriven_2);
  and and_5 (and_5_out, undriven, not_2_out);
  and and_6 (and_6_out, undriven, not_2_out);
  and and_7 (and_7_out, undriven, undriven_2);
  and and_8 (and_8_out, undriven, undriven_2);
  and and_9 (and_9_out, and_1_out, not_3_out);
  and and_10 (and_10_out, and_2_out, undriven_3);
  and and_11 (and_11_out, and_3_out, not_3_out);
  and and_12 (and_12_out, and_4_out, undriven_3);
  and and_13 (and_13_out, and_5_out, not_3_out);
  and and_14 (and_14_out, and_6_out, undriven_3);
  and and_15 (and_15_out, and_7_out, not_3_out);
  and and_16 (and_16_out, and_8_out, undriven_3);

  // Notes on the sheet:
  //   In
  //   1
  //   2
  //   0
  //   Out
  //   3
  //   4
  //   5
  //   6
  //   7
endmodule
