// Digital circuit 4 to 16 line decoder.dig as structural Verilog
module _4_to_16_line_decoder (
);

  wire and_1_out, and_2_out, and_3_out, and_4_out, and_5_out, and_6_out, and_7_out, and_8_out, and_9_out,
       and_10_out, and_11_out, and_12_out, and_13_out, and_14_out, and_15_out, and_16_out, and_17_out,
       and_18_out, and_19_out, and_20_out, and_21_out, and_22_out, and_23_out, and_24_out, and_25_out,
       and_26_out, and_27_out, and_28_out, and_29_out, and_30_out, and_31_out, and_32_out, and_33_out,
       and_34_out, and_35_out, and_36_out, and_37_out, and_38_out, and_39_out, and_40_out, and_41_out,
       and_42_out, and_43_out, and_44_out, and_45_out, and_46_out, and_47_out, and_48_out, not_1_out,
       not_2_out, not_3_out, not_4_out, undriven, undriven_2, undriven_3, undriven_4;

  not not_1 (not_1_out, undriven_2);
  not not_2 (not_2_out, undriven);
  not not_3 (not_3_out, undriven_4);
  not not_4 (not_4_out, undriven_3);
  and and_1 (and_1_out, not_2_out, not_1_out);
  and and_2 (and_2_out, not_2_out, not_1_out);
  and and_3 (and_3_out, not_2_out, not_1_out);
  and and_4 (and_4_out, not_2_out, not_1_out);
  and and_5 (and_5_out, not_2_out, undriven_2);
  and and_6 (and_6_out, not_2_out, undriven_2);
  and and_7 (and_7_out, not_2_out, undriven_2);
  and and_8 (and_8_out, not_2_out, undriven_2);
  and and_9 (and_9_out, undriven, not_1_out);
  and and_10 (and_10_out, undriven, not_1_out);
  and and_11 (and_11_out, undriven, not_1_out);
  and and_12 (and_12_out, undriven, not_1_out);
  and and_13 (and_13_out, undriven, undriven_2);
  and and_14 (and_14_out, undriven, undriven_2);
  and and_15 (and_15_out, undriven, undriven_2);
  and and_16 (and_16_out, undriven, undriven_2);
  and and_17 (and_17_out, and_1_out, not_4_out);
  and and_18 (and_18_out, and_2_out, not_4_out);
  and and_19 (and_19_out, and_3_out, undriven_3);
  and and_20 (and_20_out, and_4_out, undriven_3);
  and and_21 (and_21_out, and_5_out, not_4_out);
  and and_22 (and_22_out, and_6_out, not_4_out);
  and and_23 (and_23_out, and_7_out, undriven_3);
  and and_24 (and_24_out, and_8_out, undriven_3);
  and and_25 (and_25_out, and_9_out, not_4_out);
  and and_26 (and_26_out, and_10_out, not_4_out);
  and and_27 (and_27_out, and_11_out, undriven_3);
  and and_28 (and_28_out, and_12_out, undriven_3);
  and and_29 (and_29_out, and_13_out, not_4_out);
  and and_30 (and_30_out, and_14_out, not_4_out);
  and and_31 (and_31_out, and_15_out, undriven_3);
  and and_32 (and_32_out, and_16_out, undriven_3);
  and and_33 (and_33_out, and_17_out, not_3_out);
  and and_34 (and_34_out, and_18_out, undriven_4);
  and and_35 (and_35_out, and_19_out, not_3_out);
  and and_36 (and_36_out, and_20_out, undriven_4);
  and and_37 (and_37_out, and_21_out, not_3_out);
  and and_38 (and_38_out, and_22_out, undriven_4);
  and and_39 (and_39_out, and_23_out, not_3_out);
  and and_40 (and_40_out, and_24_out, undriven_4);
  and and_41 (and_41_out, and_25_out, not_3_out);
  and and_42 (and_42_out, and_26_out, undriven_4);
  and and_43 (and_43_out, and_27_out, not_3_out);
  and and_44 (and_44_out, and_28_out, undriven_4);
  and and_45 (and_45_out, and_29_out, not_3_out);
  and and_46 (and_46_out, and_30_out, undriven_4);
  and and_47 (and_47_out, and_31_out, not_3_out);
  and and_48 (and_48_out, and_32_out, undriven_4);

  // Notes on the sheet:
  //   In
  //   3
  //   2
  //   1
  //   0
  //   Out
  //   4
  //   5
  //   6
  //   7
  //   8
  //   9
  //   10
  //   11
  //   12
  //   13
  //   14
  //   15
endmodule
