// Digital circuit 1x2 demultiplexer.dig as structural Verilog
module _1x2_demultiplexer (
);

  wire and_1_out, and_2_out, not_1_out, undriven, undriven_2;

  not not_1 (not_1_out, undriven_2);
  and and_1 (and_1_out, undriven, not_1_out);
  and and_2 (and_2_out, undriven_2, undriven);

  // Notes on the sheet:
  //   Selection
  //   Input
  //   Out
  //   0
  //   1
endmodule
