// Digital circuit 1x4 demultiplexer.dig as structural Verilog
module _1x4_demultiplexer (
);

  wire and_1_out, and_2_out, and_3_out, and_4_out, and_5_out, and_6_out, and_7_out, and_8_out, not_1_out,
       not_2_out, undriven, undriven_2, undriven_3;

  not not_1 (not_1_out, undriven_2);
  not not_2 (not_2_out, undriven_3);
  and and_1 (and_1_out, not_2_out, undriven);
  and and_2 (and_2_out, undriven_3, undriven);
  and and_3 (and_3_out, undriven_2, undriven);
  and and_4 (and_4_out, undriven_2, undriven);
  and and_5 (and_5_out, and_1_out, not_1_out);
  and and_6 (and_6_out, and_2_out, not_1_out);
  and and_7 (and_7_out, and_3_out, not_2_out);
  and and_8 (and_8_out, and_4_out, undriven_3);

  // Notes on the sheet:
  //   Input
  //   S
  //   1
  //   0
  //   Out
  //   2
  //   3
endmodule
