// Digital circuit Binary cell.dig as structural Verilog
module Binary_cell (
);

  wire and_1_out, and_2_out, and_3_out, and_4_out, and_5_out, and_6_out, nor_1_out, nor_2_out, not_1_out,
       not_2_out, undriven, undriven_2, undriven_3;

  not not_1 (not_1_out, undriven);
  and and_1 (and_1_out, undriven_2, not_1_out);
  and and_2 (and_2_out, undriven_2, undriven);
  and and_3 (and_3_out, and_1_out, not_2_out);
  and and_4 (and_4_out, and_2_out, not_2_out);
  not not_2 (not_2_out, undriven_3);
  nor nor_1 (nor_1_out, and_3_out, nor_2_out);
  nor nor_2 (nor_2_out, nor_1_out, and_4_out);
  and and_5 (and_5_out, undriven_2, nor_1_out);
  and and_6 (and_6_out, and_5_out, undriven_3);

  // Notes on the sheet:
  //   Input
  //   Select
  //   Read/Write
  //   Output
endmodule
