// Digital circuit 2x1 multiplexer.dig as structural Verilog
module _2x1_multiplexer (
);

  wire and_1_out, and_2_out, not_1_out, or_1_out, undriven, undriven_2, undriven_3;

  and and_1 (and_1_out, undriven, not_1_out);
  not not_1 (not_1_out, undriven_3);
  and and_2 (and_2_out, undriven_3, undriven_2);
  or or_1 (or_1_out, and_1_out, and_2_out);

  // Notes on the sheet:
  //   Input
  //   Selection
  //   Output
endmodule
