// Digital circuit 4x1 multiplexer.dig as structural Verilog
module _4x1_multiplexer (
);

  wire and_1_out, and_2_out, and_3_out, and_4_out, and_5_out, and_6_out, and_7_out, and_8_out, not_1_out,
       not_2_out, or_1_out, or_2_out, or_3_out, undriven, undriven_2, undriven_3, undriven_4, undriven_5,
       undriven_6;

  not not_1 (not_1_out, undriven_5);
  not not_2 (not_2_out, undriven_6);
  and and_1 (and_1_out, not_2_out, undriven);
  and and_2 (and_2_out, undriven_6, undriven_2);
  and and_3 (and_3_out, undriven_5, undriven_3);
  and and_4 (and_4_out, undriven_5, undriven_4);
  and and_5 (and_5_out, and_1_out, not_1_out);
  and and_6 (and_6_out, and_2_out, not_1_out);
  and and_7 (and_7_out, and_3_out, not_2_out);
  and and_8 (and_8_out, and_4_out, undriven_6);
  or or_1 (or_1_out, and_5_out, and_6_out);
  or or_2 (or_2_out, and_7_out, and_8_out);
  or or_3 (or_3_out, or_1_out, or_2_out);

  // Notes on the sheet:
  //   S
  //   In
  //   0
  //   1
  //   2
  //   3
  //   Out
endmodule
